// Logisim project Adders.circ as structural Verilog
module FA0 (
  input  a,
  input  b,
  output s,
  output c
);

  wire nor_1_out;

  nor nor_1 (nor_1_out, a, b);
  and and_1 (c, b, a);
  nor nor_2 (s, nor_1_out, c);

  // Notes on the sheet:
  //   14 transistors
  //   1.75
  //   Optimized half adder 
  //   Rio Blumenthal
  //   2.75
endmodule

module FA1 (
  input  a,
  input  b,
  output s,
  output c
);

  wire nand_1_out;

  or or_1 (c, a, b);
  nand nand_1 (nand_1_out, b, a);
  nand nand_2 (s, c, nand_1_out);

  // Notes on the sheet:
  //   14 transistors
  //   1.75
  //   Optimized FA1 
  //   Rio Blumenthal
  //   2.75
endmodule

module FAopt1 (
  input  a,
  input  b,
  input  Cin,
  output SUM,
  output Cout
);

  wire nand_1_out, nand_2_out, nor_1_out, nor_2_out, nor_3_out, not_1_out, not_2_out;

  nor nor_1 (nor_1_out, a, b);
  not not_1 (not_1_out, nand_1_out);
  nand nand_1 (nand_1_out, b, a);
  nor nor_2 (nor_2_out, nor_1_out, not_1_out);
  nor nor_3 (nor_3_out, nor_2_out, Cin);
  nand nand_2 (nand_2_out, nor_2_out, Cin);
  nor nor_4 (SUM, nor_3_out, not_2_out);
  not not_2 (not_2_out, nand_2_out);
  nand nand_3 (Cout, nand_2_out, nand_1_out);

  // Notes on the sheet:
  //   0
  //   0
  //   32 transistors
  //   if Cin < 2.75, S = 5.5, else S = Cin + 2.75
  //   FAopt1
  //   Rio Blumenthal
  //   If Cin < 2.75, Cout = 4.75, else Cout = Cin + 2
endmodule

module FAopt2 (
  input  a,
  input  b,
  input  Cin,
  output SUM,
  output Cout
);

  wire nand_1_out, nand_2_out, nand_3_out, nand_4_out, nor_1_out, nor_2_out, nor_3_out, not_1_out, not_2_out;

  nor nor_1 (nor_1_out, a, b);
  not not_1 (not_1_out, nand_1_out);
  nand nand_1 (nand_1_out, b, a);
  nor nor_2 (nor_2_out, nor_1_out, not_1_out);
  nor nor_3 (nor_3_out, nor_2_out, Cin);
  nand nand_2 (nand_2_out, nor_2_out, Cin);
  nor nor_4 (SUM, nor_3_out, not_2_out);
  not not_2 (not_2_out, nand_2_out);
  nand nand_3 (nand_3_out, Cin, b);
  nand nand_4 (nand_4_out, Cin, a);
  nand nand_5 (Cout, nand_1_out, nand_3_out, nand_4_out);

  // Notes on the sheet:
  //   0
  //   0
  //   42 transistors
  //   Cin + 2.25
  //   FAopt2
  //   if Cin < 2.75, S = 5.5, else S = Cin + 2.75
  //   Rio Blumenthal
endmodule

module adder4Bit0 (
  input  [3:0] in_1,
  input  [3:0] in_2,
  output [3:0] _8_75,
  output _8
);

  wire fa0_1_c, faopt1_2_cout, faopt2_1_cout;

  FAopt1 faopt1_1 (.a(in_1[3]), .b(in_2[3]), .Cin(faopt1_2_cout), .SUM(_8_75[3]), .Cout(_8));
  FAopt1 faopt1_2 (.a(in_1[2]), .b(in_2[2]), .Cin(faopt2_1_cout), .SUM(_8_75[2]), .Cout(faopt1_2_cout));
  FAopt2 faopt2_1 (.a(in_1[1]), .b(in_2[1]), .Cin(fa0_1_c), .SUM(_8_75[1]), .Cout(faopt2_1_cout));
  FA0 fa0_1 (.a(in_2[0]), .b(in_1[0]), .s(_8_75[0]), .c(fa0_1_c));

  // Notes on the sheet:
  //   8
  //   8.75
  //   120 transistors
  //   4-Bit Adder
  //   Rio Blumenthal
  //   6
  //   6.75
  //   4
  //   5.5
  //   1.75
  //   2.75
endmodule

module adder8BitRipple (
  input  [7:0] in_1,
  input  [7:0] in_2,
  output [7:0] _16_75,
  output _16
);

  wire fa0_1_c, faopt1_2_cout, faopt1_3_cout, faopt1_4_cout, faopt1_5_cout, faopt1_6_cout, faopt2_1_cout;

  FAopt1 faopt1_1 (.a(in_1[7]), .b(in_2[7]), .Cin(faopt1_2_cout), .SUM(_16_75[7]), .Cout(_16));
  FAopt1 faopt1_2 (.a(in_1[6]), .b(in_2[6]), .Cin(faopt1_3_cout), .SUM(_16_75[6]), .Cout(faopt1_2_cout));
  FAopt1 faopt1_3 (.a(in_1[5]), .b(in_2[5]), .Cin(faopt1_4_cout), .SUM(_16_75[5]), .Cout(faopt1_3_cout));
  FAopt1 faopt1_4 (.a(in_1[4]), .b(in_2[4]), .Cin(faopt1_5_cout), .SUM(_16_75[4]), .Cout(faopt1_4_cout));
  FAopt1 faopt1_5 (.a(in_1[3]), .b(in_2[3]), .Cin(faopt1_6_cout), .SUM(_16_75[3]), .Cout(faopt1_5_cout));
  FAopt1 faopt1_6 (.a(in_1[2]), .b(in_2[2]), .Cin(faopt2_1_cout), .SUM(_16_75[2]), .Cout(faopt1_6_cout));
  FAopt2 faopt2_1 (.a(in_1[1]), .b(in_2[1]), .Cin(fa0_1_c), .SUM(_16_75[1]), .Cout(faopt2_1_cout));
  FA0 fa0_1 (.a(in_2[0]), .b(in_1[0]), .s(_16_75[0]), .c(fa0_1_c));

  // Notes on the sheet:
  //   16
  //   248 transistors
  //   8-Bit Adder
  //   Rio Blumenthal
  //   14
  //   16.75
  //   12
  //   14.75
  //   10
  //   12.75
  //   8
  //   10.75
  //   6
  //   8.75
  //   6.75
  //   4
  //   5.5
  //   1.75
  //   2.75
endmodule

module mux2 (
  input  in0,
  input  S,
  input  in1,
  output Z
);

  wire nand_1_out, nand_2_out, not_1_out;

  not not_1 (not_1_out, S);
  nand nand_1 (nand_1_out, in0, not_1_out);
  nand nand_2 (nand_2_out, S, in1);
  nand nand_3 (Z, nand_1_out, nand_2_out);

  // Notes on the sheet:
  //   2:1 mux 
  //   Rio Blumenthal
  //   14 transistors
  //   Timing    z = max(s+2.75, in0+2, in1+2)
endmodule

module mx2i (
  input  ln0,
  input  ln1,
  input  S,
  output Z
);

  wire not_1_out, transmission_1_p4;

  not not_1 (not_1_out, S);
  // Transmission_Gate transmission_1: pin names not known; wires that end beside it: ln0, S, not_1_out, transmission_1_p4
  not not_2 (Z, transmission_1_p4);
  // Transmission_Gate transmission_2: pin names not known; wires that end beside it: ln1, not_1_out, S, transmission_1_p4

  // Notes on the sheet:
  //   Rio Blumenthal
  //   2:1 mux inverted
  //   8 transistors
  //   Timing    z = max(s+1.75, in0+1, in1+1)
endmodule

module mx4 (
  input  in0,
  input  in1,
  input  S0,
  input  in2,
  input  in3,
  input  S1,
  output Z
);

  wire mux2_1_z, mux2_2_z;

  mux2 mux2_1 (.S(S0), .in1(in2), .in0(in0), .Z(mux2_1_z));
  mux2 mux2_2 (.S(S0), .in1(in3), .in0(in1), .Z(mux2_2_z));
  mux2 mux2_3 (.S(S1), .in1(mux2_2_z), .in0(mux2_1_z), .Z(Z));

  // Notes on the sheet:
  //   Rio Blumenthal
  //   4:1 mux no transmission gates
  //   42 transistors
  //   Timing    z = max(s0 + 4.75, s1 + 2.75, in0+4, in1+4, in2+4, in3+4)
endmodule

module mx4trans (
  input  in0,
  input  in1,
  input  S0,
  input  in2,
  input  in3,
  input  S1,
  output Z
);

  wire mx2i_1_z, mx2i_2_z;

  mx2i mx2i_1 (.ln1(in2), .ln0(in0), .Z(mx2i_1_z));  // open: S
  mx2i mx2i_2 (.ln1(in3), .ln0(in1), .Z(mx2i_2_z));  // open: S
  mx2i mx2i_3 (.ln1(mx2i_2_z), .ln0(mx2i_1_z), .Z(Z));  // open: S

  // Notes on the sheet:
  //   4:1 mux with transmission gates
  //   Rio Blumenthal
  //   24 transistors
  //   Timing    z = max(s0 + 2.75, s1 + 1.75, in0+2, in1+2, in2+2, in3+2)
endmodule

module adder8BitCarrySelect0 (
  input  [7:0] a,
  input  [7:0] b,
  output [7:0] sum,
  output cout
);

  wire adder4bit0_1__8, adder4bit0_2__8, adder4bit1_1__8, mx2i_1_z;
  wire [3:0] adder4bit0_1__8_75, adder4bit1_1__8_75, mx2i_4_1_out_4;

  mx2i mx2i_1 (.ln1(adder4bit1_1__8), .S(adder4bit0_2__8), .ln0(adder4bit0_1__8), .Z(mx2i_1_z));
  adder4Bit1 adder4bit1_1 (.in_1(a[7:4]), .in_2(b[7:4]), ._8_75(adder4bit1_1__8_75), ._8(adder4bit1_1__8));
  adder4Bit0 adder4bit0_1 (.in_1(a[7:4]), .in_2(b[7:4]), ._8_75(adder4bit0_1__8_75), ._8(adder4bit0_1__8));
  mx2i_4 mx2i_4_1 (.s(adder4bit0_2__8), .in0(adder4bit0_1__8_75), .in1(adder4bit1_1__8_75), .out_4(mx2i_4_1_out_4));
  assign sum[7:4] = ~mx2i_4_1_out_4;  // NOT_Gate not_1, 4 bits wide
  adder4Bit0 adder4bit0_2 (.in_1(a[3:0]), .in_2(b[3:0]), ._8_75(sum[3:0]), ._8(adder4bit0_2__8));
  not not_2 (cout, mx2i_1_z);

  // Notes on the sheet:
  //   8
  //   Rio Blumenthal
  //   adder8bitCarrySelect0
  //   8
  //   8.75
  //   9.75
  //   9.75
  //   8.75
  //   8
  //   8.75
  //   10.5
  //   10.5
endmodule

module mx2i_4 (
  input  [3:0] in1,
  input  [3:0] in0,
  input  s,
  output [3:0] out_4
);

  mx2i mx2i_1 (.ln1(in1[0]), .S(s), .ln0(in0[0]), .Z(out_4[0]));
  mx2i mx2i_2 (.ln1(in1[1]), .S(s), .ln0(in0[1]), .Z(out_4[1]));
  mx2i mx2i_3 (.ln1(in1[2]), .S(s), .ln0(in0[2]), .Z(out_4[2]));
  mx2i mx2i_4 (.ln1(in1[3]), .S(s), .ln0(in0[3]), .Z(out_4[3]));
endmodule

module adder4Bit1 (
  input  [3:0] in_1,
  input  [3:0] in_2,
  output [3:0] _8_75,
  output _8
);

  wire fa1_1_c, faopt1_2_cout, faopt2_1_cout;

  FAopt1 faopt1_1 (.a(in_1[3]), .b(in_2[3]), .Cin(faopt1_2_cout), .SUM(_8_75[3]), .Cout(_8));
  FAopt1 faopt1_2 (.a(in_1[2]), .b(in_2[2]), .Cin(faopt2_1_cout), .SUM(_8_75[2]), .Cout(faopt1_2_cout));
  FAopt2 faopt2_1 (.a(in_1[1]), .b(in_2[1]), .Cin(fa1_1_c), .SUM(_8_75[1]), .Cout(faopt2_1_cout));
  FA1 fa1_1 (.a(in_2[0]), .b(in_1[0]), .s(_8_75[0]), .c(fa1_1_c));

  // Notes on the sheet:
  //   8
  //   8.75
  //   120 transistors
  //   4-Bit Adder
  //   Rio Blumenthal
  //   6
  //   6.75
  //   4
  //   5.5
  //   1.75
  //   2.75
endmodule

module adder8BitCarrySelect1 (
  input  [7:0] a,
  input  [7:0] b,
  output [7:0] sum,
  output cout
);

  wire adder4bit0_1__8, adder4bit1_1__8, adder4bit1_2__8, mx2i_1_z;
  wire [3:0] adder4bit0_1__8_75, adder4bit1_1__8_75, mx2i_4_1_out_4;

  mx2i mx2i_1 (.ln1(adder4bit1_1__8), .S(adder4bit1_2__8), .ln0(adder4bit0_1__8), .Z(mx2i_1_z));
  adder4Bit1 adder4bit1_1 (.in_1(a[7:4]), .in_2(b[7:4]), ._8_75(adder4bit1_1__8_75), ._8(adder4bit1_1__8));
  adder4Bit0 adder4bit0_1 (.in_1(a[7:4]), .in_2(b[7:4]), ._8_75(adder4bit0_1__8_75), ._8(adder4bit0_1__8));
  mx2i_4 mx2i_4_1 (.s(adder4bit1_2__8), .in0(adder4bit0_1__8_75), .in1(adder4bit1_1__8_75), .out_4(mx2i_4_1_out_4));
  assign sum[7:4] = ~mx2i_4_1_out_4;  // NOT_Gate not_1, 4 bits wide
  adder4Bit1 adder4bit1_2 (.in_1(a[3:0]), .in_2(b[3:0]), ._8_75(sum[3:0]), ._8(adder4bit1_2__8));
  not not_2 (cout, mx2i_1_z);

  // Notes on the sheet:
  //   8
  //   Rio Blumenthal
  //   adder8bitCarrySelect1
  //   8
  //   8.75
  //   9.75
  //   9.75
  //   8.75
  //   8
  //   8.75
  //   10.5
  //   10.5
endmodule

module mx2i_8 (
  input  [7:0] in0,
  input  [7:0] in1,
  input  in_3,
  output [7:0] out_4
);

  mx2i_4 mx2i_4_1 (.s(in_3), .in0(in0[3:0]), .in1(in1[3:0]), .out_4(out_4[3:0]));
  mx2i_4 mx2i_4_2 (.s(in_3), .in0(in0[7:4]), .in1(in1[7:4]), .out_4(out_4[7:4]));
endmodule

module adder16BitCarrySelect (
  input  [15:0] a,
  input  [15:0] b,
  output [15:0] sum,
  output cout
);

  wire adder8bitcarryselect0_1_cout, adder8bitcarryselect0_2_cout, adder8bitcarryselect1_1_cout, mx2i_1_z;
  wire [7:0] adder8bitcarryselect0_1_sum, adder8bitcarryselect1_1_sum, mx2i_8_1_out_4;

  mx2i mx2i_1 (
    .ln1(adder8bitcarryselect1_1_cout), .S(adder8bitcarryselect0_2_cout), .ln0(adder8bitcarryselect0_1_cout),
    .Z(mx2i_1_z));
  adder8BitCarrySelect1 adder8bitcarryselect1_1 (
    .a(a[15:8]), .b(b[15:8]), .sum(adder8bitcarryselect1_1_sum), .cout(adder8bitcarryselect1_1_cout));
  adder8BitCarrySelect0 adder8bitcarryselect0_1 (
    .a(a[15:8]), .b(b[15:8]), .sum(adder8bitcarryselect0_1_sum), .cout(adder8bitcarryselect0_1_cout));
  mx2i_8 mx2i_8_1 (
    .in0(adder8bitcarryselect0_1_sum), .in1(adder8bitcarryselect1_1_sum),
    .in_3(adder8bitcarryselect0_2_cout), .out_4(mx2i_8_1_out_4));
  assign sum[15:8] = ~mx2i_8_1_out_4;  // NOT_Gate not_1, 8 bits wide
  adder8BitCarrySelect0 adder8bitcarryselect0_2 (
    .a(a[7:0]), .b(b[7:0]), .sum(sum[7:0]), .cout(adder8bitcarryselect0_2_cout));
  not not_2 (cout, mx2i_1_z);

  // Notes on the sheet:
  //   10.5
  //   Rio Blumenthal
  //   adder16bitCarrySelect0
  //   10/5
  //   10.5
  //   12.25
  //   12.25
  //   10.5
  //   10.5
  //   10.5
  //   13
  //   16 bit ripple adder = 16+16.75 = 32.75 sum, 32 carry
  //   13
endmodule

module CLAC4num1 (
  input  G0,
  input  G1,
  input  G2,
  input  G3,
  input  P0,
  input  P1,
  input  P2,
  input  P3,
  input  C0,
  output out_10
);

  wire and_1_out, and_2_out, and_3_out, and_4_out;

  and and_1 (and_1_out, P3, G2);
  and and_2 (and_2_out, P3, G1, P0);
  and and_3 (and_3_out, G0, P0, P0, P3);
  and and_4 (and_4_out, P0, P0, P0, P3, C0);
  or or_1 (out_10, and_1_out, and_2_out, G3, and_3_out, and_4_out);

  assign P1 = P0;
  assign P2 = P0;
endmodule

module CLAC4num2 (
  input  P0,
  input  P1,
  input  P2,
  input  P3,
  input  G2,
  input  G1,
  input  G0,
  input  G3,
  input  C0,
  output _4_25
);

  wire nand_1_out, nand_2_out, nand_3_out, nand_4_out, nor_1_out, nor_2_out, nor_3_out, nor_4_out, nor_5_out,
       nor_6_out, not_1_out, not_2_out, not_3_out, not_4_out, not_5_out;

  not not_1 (not_1_out, P3);
  not not_2 (not_2_out, G2);
  not not_3 (not_3_out, P3);
  not not_4 (not_4_out, P2);
  not not_5 (not_5_out, G1);
  nor nor_1 (nor_1_out, not_1_out, not_2_out);
  nor nor_2 (nor_2_out, not_3_out, not_4_out, not_5_out);
  nand nand_1 (nand_1_out, G0, P3);
  nand nand_2 (nand_2_out, P2, P1);
  nand nand_3 (nand_3_out, P3, C0);
  nand nand_4 (nand_4_out, P1, P2, P0);
  nor nor_3 (nor_3_out, nand_1_out, nand_2_out);
  nor nor_4 (nor_4_out, nand_3_out, nand_4_out);
  nor nor_5 (nor_5_out, nor_1_out, nor_2_out);
  nor nor_6 (nor_6_out, nor_3_out, nor_4_out, G3);
  nand nand_5 (_4_25, nor_5_out, nor_6_out);

  // Notes on the sheet:
  //   1
  //   2
  //   Rio Blumenthal
  //   CLAC4num2
  //   3.25
endmodule

module CLAC4num3 (
  input  P0,
  input  P1,
  input  P2,
  input  P3,
  input  G2,
  input  C0,
  input  G1,
  input  G0,
  input  G3,
  output out_10
);

  wire aoi21_1_out_4, nand_1_out, nand_2_out, nand_3_out, nand_4_out, nand_5_out, nor_1_out, nor_2_out,
       nor_3_out, nor_4_out, nor_5_out, nor_6_out, not_1_out, not_2_out, not_3_out, not_4_out, not_5_out;

  not not_1 (not_1_out, P3);
  not not_2 (not_2_out, G2);
  not not_3 (not_3_out, P3);
  not not_4 (not_4_out, P2);
  not not_5 (not_5_out, G1);
  nor nor_1 (nor_1_out, not_1_out, not_2_out);
  nor nor_2 (nor_2_out, not_3_out, not_4_out, not_5_out);
  nand nand_1 (nand_1_out, G0, P3);
  nand nand_2 (nand_2_out, P2, P1);
  nand nand_3 (nand_3_out, P3, P2);
  nand nand_4 (nand_4_out, P1, P0);
  nor nor_3 (nor_3_out, nand_1_out, nand_2_out);
  nor nor_4 (nor_4_out, nand_3_out, nand_4_out);
  nor nor_5 (nor_5_out, nor_1_out, nor_2_out);
  nor nor_6 (nor_6_out, nor_3_out, G3);
  nand nand_5 (nand_5_out, nor_5_out, nor_6_out);
  AOI21 aoi21_1 (.C(C0), .Y(nor_4_out), .X(nand_5_out), .out_4(aoi21_1_out_4));
  not not_6 (out_10, aoi21_1_out_4);
endmodule

module AOI21 (
  input  C,
  input  Y,
  input  X,
  output out_4
);

  wire transistor_1_out, transistor_6_out;

  Transistor transistor_1 (.in(1'b1), .out(transistor_1_out), .gate(Y));
  Transistor transistor_2 (.in(transistor_1_out), .out(out_4), .gate(X));
  Transistor #(.\type ("n")) transistor_3 (.in(1'b0), .out(out_4), .gate(X));
  Transistor transistor_4 (.in(1'b1), .out(transistor_1_out), .gate(C));
  Transistor #(.\type ("n")) transistor_5 (.in(transistor_6_out), .out(out_4), .gate(Y));
  Transistor #(.\type ("n")) transistor_6 (.in(1'b0), .out(transistor_6_out), .gate(C));
endmodule

module adderSubtract (
  input  [15:0] A,
  input  [15:0] B,
  input  in_3,
  output [15:0] out_4,
  output out_5
);

  wire nand_1_out, nand_2_out, not_2_out, not_3_out, not_4_out, not_5_out;
  wire [15:0] multiplexer_1_out, not_1_out;

  nand nand_1 (nand_1_out, A[15], multiplexer_1_out[15], not_5_out);
  assign not_1_out = ~B;  // NOT_Gate not_1, 16 bits wide
  not not_2 (not_2_out, multiplexer_1_out[15]);
  not not_3 (not_3_out, A[15]);
  nand nand_2 (nand_2_out, not_2_out, not_3_out, out_4[15]);
  Multiplexer #(.width(16)) multiplexer_1 (.in0(not_1_out), .in1(B), .out(multiplexer_1_out), .sel(not_4_out));
  not not_4 (not_4_out, in_3);
  nand nand_3 (out_5, nand_2_out, nand_1_out);
  Adder #(.width(16)) adder_1 (.a(A), .b(multiplexer_1_out), .out(out_4), .cin(in_3));  // open: cout
  not not_5 (not_5_out, out_4[15]);
endmodule

module adderSubtractorHomecooker (
  input  [15:0] A,
  input  [15:0] B,
  input  in_3,
  output [15:0] out_4,
  output out_5
);

  wire nand_1_out, nand_2_out, not_2_out, not_3_out, not_4_out, not_5_out;
  wire [15:0] multiplexer_1_out, not_1_out;

  nand nand_1 (nand_1_out, A[15], multiplexer_1_out[15], not_5_out);
  assign not_1_out = ~B;  // NOT_Gate not_1, 16 bits wide
  not not_2 (not_2_out, multiplexer_1_out[15]);
  not not_3 (not_3_out, A[15]);
  nand nand_2 (nand_2_out, not_2_out, not_3_out, out_4[15]);
  Multiplexer #(.width(16)) multiplexer_1 (.in0(not_1_out), .in1(B), .out(multiplexer_1_out), .sel(not_4_out));
  not not_4 (not_4_out, in_3);
  nand nand_3 (out_5, nand_2_out, nand_1_out);
  adder16BitCarrySelect2 adder16bitcarryselect2_1 (
    .a(A), .b(multiplexer_1_out), .in_3(in_3), .sum(out_4));  // open: cout
  not not_5 (not_5_out, out_4[15]);
endmodule

module adder4Bit2 (
  input  [3:0] A,
  input  [3:0] B,
  input  Cin,
  output [3:0] S,
  output Cout
);

  wire faopt1_2_cout, faopt2_1_cout, faopt2_2_cout;

  FAopt1 faopt1_1 (.a(A[3]), .b(B[3]), .Cin(faopt1_2_cout), .SUM(S[3]), .Cout(Cout));
  FAopt1 faopt1_2 (.a(A[2]), .b(B[2]), .Cin(faopt2_1_cout), .SUM(S[2]), .Cout(faopt1_2_cout));
  FAopt2 faopt2_1 (.a(A[1]), .b(B[1]), .Cin(faopt2_2_cout), .SUM(S[1]), .Cout(faopt2_1_cout));
  FAopt2 faopt2_2 (.a(A[0]), .b(B[0]), .Cin(Cin), .SUM(S[0]), .Cout(faopt2_2_cout));

  // Notes on the sheet:
  //   8
  //   8.75
  //   120 transistors
  //   4-Bit Adder
  //   Rio Blumenthal
  //   6
  //   6.75
  //   4
  //   5.5
  //   1.75
  //   2.75
  //   8.75
  //   8
endmodule

module adder8BitCarrySelect2 (
  input  [7:0] a,
  input  [7:0] b,
  input  in_3,
  output [7:0] sum,
  output cout
);

  wire adder4bit0_1__8, adder4bit1_1__8, adder4bit2_1_cout, mx2i_1_z;
  wire [3:0] adder4bit0_1__8_75, adder4bit1_1__8_75, mx2i_4_1_out_4;

  mx2i mx2i_1 (.ln1(adder4bit1_1__8), .S(adder4bit2_1_cout), .ln0(adder4bit0_1__8), .Z(mx2i_1_z));
  adder4Bit1 adder4bit1_1 (.in_1(a[7:4]), .in_2(b[7:4]), ._8_75(adder4bit1_1__8_75), ._8(adder4bit1_1__8));
  adder4Bit0 adder4bit0_1 (.in_1(a[7:4]), .in_2(b[7:4]), ._8_75(adder4bit0_1__8_75), ._8(adder4bit0_1__8));
  mx2i_4 mx2i_4_1 (.s(adder4bit2_1_cout), .in0(adder4bit0_1__8_75), .in1(adder4bit1_1__8_75), .out_4(mx2i_4_1_out_4));
  assign sum[7:4] = ~mx2i_4_1_out_4;  // NOT_Gate not_1, 4 bits wide
  adder4Bit2 adder4bit2_1 (.A(b[3:0]), .B(a[3:0]), .Cin(in_3), .S(sum[3:0]), .Cout(adder4bit2_1_cout));
  not not_2 (cout, mx2i_1_z);

  // Notes on the sheet:
  //   8
  //   Rio Blumenthal
  //   adder8bitCarrySelect1
  //   8
  //   8.75
  //   9.75
  //   9.75
  //   8.75
  //   8
  //   8.75
  //   10.5
  //   10.5
endmodule

module adder16BitCarrySelect2 (
  input  [15:0] a,
  input  [15:0] b,
  input  in_3,
  output [15:0] sum,
  output cout
);

  wire adder8bitcarryselect0_1_cout, adder8bitcarryselect1_1_cout, adder8bitcarryselect2_1_cout, mx2i_1_z;
  wire [7:0] adder8bitcarryselect0_1_sum, adder8bitcarryselect1_1_sum, mx2i_8_1_out_4;

  mx2i mx2i_1 (
    .ln1(adder8bitcarryselect1_1_cout), .S(adder8bitcarryselect2_1_cout), .ln0(adder8bitcarryselect0_1_cout),
    .Z(mx2i_1_z));
  adder8BitCarrySelect1 adder8bitcarryselect1_1 (
    .a(a[15:8]), .b(b[15:8]), .sum(adder8bitcarryselect1_1_sum), .cout(adder8bitcarryselect1_1_cout));
  adder8BitCarrySelect0 adder8bitcarryselect0_1 (
    .a(a[15:8]), .b(b[15:8]), .sum(adder8bitcarryselect0_1_sum), .cout(adder8bitcarryselect0_1_cout));
  mx2i_8 mx2i_8_1 (
    .in0(adder8bitcarryselect0_1_sum), .in1(adder8bitcarryselect1_1_sum),
    .in_3(adder8bitcarryselect2_1_cout), .out_4(mx2i_8_1_out_4));
  assign sum[15:8] = ~mx2i_8_1_out_4;  // NOT_Gate not_1, 8 bits wide
  adder8BitCarrySelect2 adder8bitcarryselect2_1 (
    .a(a[7:0]), .b(b[7:0]), .in_3(in_3), .sum(sum[7:0]), .cout(adder8bitcarryselect2_1_cout));
  not not_2 (cout, mx2i_1_z);

  // Notes on the sheet:
  //   10.5
  //   Rio Blumenthal
  //   adder16bitCarrySelect0
  //   10/5
  //   10.5
  //   12.25
  //   12.25
  //   10.5
  //   10.5
  //   10.5
  //   13
  //   16 bit ripple adder = 16+16.75 = 32.75 sum, 32 carry
  //   13
endmodule

module LALU (
  input  RST,
  input  sub,
  input  [15:0] in_3,
  output [15:0] out_4,
  output [15:0] out_5
);

  wire clk;
  wire [15:0] sum;

  Clock u_CLK (.out(clk));
  Register #(.width(16)) R1 (.D(in_3), .en(1'b1), .clk(clk), .Q(out_5), .clr(RST));
  Register #(.width(16)) R0 (.D(sum), .en(1'b1), .clk(clk), .Q(out_4), .clr(RST));
  adderSubtractorHomecooker addersubtractorhomecooker_1 (.A(out_4), .B(out_5), .in_3(sub), .out_4(sum));  // open: out_5

  // Other names for the same wires on the sheet: r0[15:0] = out_4; r1[15:0] = out_5
endmodule

module regWE (
  input  regWrite,
  input  [1:0] Rd,
  output reg0WE,
  output reg1WE,
  output reg2WE,
  output reg3WE
);

  wire not_1_out, not_2_out, not_3_out;

  not not_1 (not_1_out, regWrite);
  not not_2 (not_2_out, Rd[0]);
  not not_3 (not_3_out, Rd[1]);
  nor nor_1 (reg0WE, not_1_out, Rd[0], Rd[1]);
  nor nor_2 (reg1WE, not_1_out, Rd[1], not_2_out);
  nor nor_3 (reg2WE, not_1_out, not_3_out, Rd[0]);
  nor nor_4 (reg3WE, not_1_out, not_2_out, not_3_out);
endmodule

module srcSel (
  input  [15:0] reg0,
  input  [15:0] reg1,
  input  [15:0] reg2,
  input  [15:0] reg3,
  input  [1:0] sel,
  output [15:0] out_6
);

  wire [15:0] multiplexer_1_out, multiplexer_2_out;

  Multiplexer #(.width(16)) multiplexer_1 (.in0(reg0), .in1(reg1), .out(multiplexer_1_out), .sel(sel[0]));
  Multiplexer #(.width(16)) multiplexer_2 (.in0(reg2), .in1(reg3), .out(multiplexer_2_out), .sel(sel[0]));
  Multiplexer #(.width(16)) multiplexer_3 (.in0(multiplexer_1_out), .in1(multiplexer_2_out), .out(out_6), .sel(sel[1]));
endmodule

module LALU2 (
  input  RST,
  output [15:0] cycles,
  output [15:0] out_3,
  output [15:0] out_4,
  output [15:0] out_5,
  output [15:0] out_6
);

  wire add, and_1_out, and_2_out, clk, GO, halt, jmp, jmpn, ld, ldi, mv, or_1_out, or_2_out, overfl,
       overfl_q, reg0WE, reg1WE, reg2WE, reg3WE, st, sub, toJump;
  wire [1:0] Rd, Rs;
  wire [3:0] register_1_q, register_1_q_2, register_2_q, register_2_q_2;
  wire [5:0] jmpData, programcounter_1_pc;
  wire [7:0] display, ram_1_dout;
  wire [15:0] dataSelector, loadOutput, multiplexer_1_out, multiplexer_2_out, RdOutput, sum, toRegister;

  Clock u_CLK (.out(clk));
  regWE regwe_1 (.regWrite(GO), .Rd(Rd), .reg0WE(reg0WE), .reg1WE(reg1WE), .reg2WE(reg2WE), .reg3WE(reg3WE));
  Hex_Digit_Display hex_digit_display_1 (.value(display[7:4]));  // open: dp
  Hex_Digit_Display hex_digit_display_2 (.value(display[3:0]));  // open: dp
  srcSel srcsel_1 (.reg0(out_3), .reg1(out_4), .reg2(out_5), .reg3(out_6), .sel(Rd), .out_6(RdOutput));
  srcSel srcsel_2 (.reg0(out_3), .reg1(out_4), .reg2(out_5), .reg3(out_6), .sel(Rs), .out_6(dataSelector));
  Register register_1 (.D(display), .en(1'b1), .clk(clk), .Q({register_1_q_2, register_1_q}), .clr(RST));
  cycleCounter cyclecounter_1 (.halt(halt), .clk(clk), .rst(RST), .cycles(cycles));
  Hex_Digit_Display hex_digit_display_3 (.value(register_1_q_2));  // open: dp
  Hex_Digit_Display hex_digit_display_4 (.value(register_1_q));  // open: dp
  Register register_2 (
    .D({register_1_q_2, register_1_q}), .en(1'b1), .clk(clk), .Q({register_2_q_2, register_2_q}), .clr(RST));
  adderSubtractorHomecooker addersubtractorhomecooker_1 (
    .A(RdOutput), .B(dataSelector), .in_3(sub), .out_5(overfl), .out_4(sum));
  Hex_Digit_Display hex_digit_display_5 (.value(register_2_q_2));  // open: dp
  Hex_Digit_Display hex_digit_display_6 (.value(register_2_q));  // open: dp
  or or_1 (or_1_out, add, sub);
  and and_1 (and_1_out, or_1_out, overfl);
  Register #(.width(16)) R0 (.D(toRegister), .en(reg0WE), .clk(clk), .Q(out_3), .clr(RST));
  Register #(.width(16)) R1 (.D(toRegister), .en(reg1WE), .clk(clk), .Q(out_4), .clr(RST));
  Register #(.width(16)) R2 (.D(toRegister), .en(reg2WE), .clk(clk), .Q(out_5), .clr(RST));
  Register #(.width(16)) R3 (.D(toRegister), .en(reg3WE), .clk(clk), .Q(out_6), .clr(RST));
  Register #(.width(1)) u_overfl (.D(1'b1), .en(and_1_out), .clk(clk), .Q(overfl_q), .clr(RST));
  LED led_1 (.in(overfl_q));
  programCounter programcounter_1 (.jmpData(jmpData), .jmp(toJump), .clk(clk), .rst(RST), .pc(programcounter_1_pc));
  Multiplexer #(.width(16)) multiplexer_1 (.in0({{14{1'b0}}, Rs}), .in1(loadOutput), .out(multiplexer_1_out), .sel(ld));
  and and_2 (and_2_out, sum[15], jmpn);
  RAM #(.addrWidth(6), .asyncread("true"), .trigger("falling")) ram_1 (
    .addr(programcounter_1_pc), .we(1'b0), .oe(1'b1), .clk(clk), .dout(ram_1_dout));  // open: din
  RAM #(.asyncread("true"), .dataWidth(16), .trigger("falling")) ram_2 (
    .addr(dataSelector[7:0]), .we(st), .oe(1'b1), .clk(clk), .din(RdOutput), .dout(loadOutput));
  or or_2 (or_2_out, add, sub);
  Multiplexer #(.width(16)) multiplexer_2 (.in0(multiplexer_1_out), .in1(sum), .out(multiplexer_2_out), .sel(or_2_out));
  or or_3 (toJump, and_2_out, jmp);
  Multiplexer #(.width(16)) multiplexer_3 (.in0(multiplexer_2_out), .in1(dataSelector), .out(toRegister), .sel(mv));
  Register register_3 (.D(ram_1_dout), .en(1'b1), .clk(clk), .Q(display), .clr(RST));
  IRdecoder irdecoder_1 (
    .IR(display), .clk(clk), .rst(RST), .Rd(Rd), .Rs(Rs), .sub(sub), .add(add), .ldi(ldi), .ld(ld), .mv(mv),
    .st(st), .jmp(jmp), .jmpn(jmpn), .jmpData(jmpData), .go(GO), .halt(halt));

  // Other names for the same wires on the sheet: R0[15:0] = out_3; R1[15:0] = out_4; R2[15:0] = out_5;
  //   R3[15:0] = out_6
endmodule

module programCounter (
  input  [5:0] jmpData,
  input  jmp,
  input  clk,
  input  rst,
  output [5:0] pc
);

  wire [5:0] adder_1_out, multiplexer_1_out;

  Adder #(.width(6)) adder_1 (.a(pc), .b(6'b000001), .out(adder_1_out));  // open: cin, cout
  Multiplexer #(.width(6)) multiplexer_1 (.in0(adder_1_out), .in1(jmpData), .out(multiplexer_1_out), .sel(jmp));
  Register #(.width(6)) register_1 (.D(multiplexer_1_out), .en(1'b1), .clk(clk), .Q(pc), .clr(rst));
endmodule

module IRdecoder (
  input  [7:0] IR,
  input  clk,
  input  rst,
  output [1:0] Rd,
  output [1:0] Rs,
  output sub,
  output add,
  output ldi,
  output ld,
  output mv,
  output st,
  output jmp,
  output jmpn,
  output [5:0] jmpData,
  output go,
  output halt
);

  wire add_t, and_6_out, and_7_out, and_8_out, and_11_out, d_ff_1_q, d_ff_2_q, ld_t, ldi_t, mv_t, not_1_out,
       not_2_out, not_3_out, not_4_out, or_1_out, sub_t;

  Register #(.width(2)) register_1 (.D(IR[7:6]), .en(1'b1), .clk(clk), .Q(Rd), .clr(rst));
  Register #(.width(2)) register_2 (.D(IR[5:4]), .en(1'b1), .clk(clk), .Q(Rs), .clr(rst));
  not not_1 (not_1_out, IR[3]);
  not not_2 (not_2_out, IR[2]);
  not not_3 (not_3_out, IR[1]);
  not not_4 (not_4_out, IR[0]);
  and and_1 (sub_t, IR[0], IR[1], not_2_out, not_1_out);
  and and_2 (add_t, not_4_out, IR[1], not_2_out, not_1_out);
  and and_3 (ldi_t, not_4_out, IR[1], IR[2], IR[3]);
  and and_4 (ld_t, IR[0], IR[1], IR[2], IR[3]);
  Register #(.width(1)) register_3 (.D(ld_t), .en(1'b1), .clk(clk), .Q(ld), .clr(rst));
  and and_5 (mv_t, not_1_out, IR[2], IR[1], not_4_out);
  and and_6 (and_6_out, IR[3], not_2_out, IR[1], IR[0]);
  and and_7 (and_7_out, not_4_out, not_3_out);
  and and_8 (and_8_out, not_3_out, IR[0]);
  Register #(.width(1)) register_4 (.D(ldi_t), .en(1'b1), .clk(clk), .Q(ldi), .clr(rst));
  Register #(.width(1)) register_5 (.D(mv_t), .en(1'b1), .clk(clk), .Q(mv), .clr(rst));
  Register #(.width(1)) register_6 (.D(and_6_out), .en(1'b1), .clk(clk), .Q(st), .clr(rst));
  Register #(.width(1)) register_7 (.D(add_t), .en(1'b1), .clk(clk), .Q(add), .clr(rst));
  D_Flip_Flop d_ff_1 (.D(1'b1), .clk(clk), .Q(d_ff_1_q), .reset(rst));  // open: Qn, preset
  D_Flip_Flop d_ff_2 (.D(1'b1), .clk(clk), .Q(d_ff_2_q), .reset(rst));  // open: Qn, preset
  Register #(.width(1)) register_8 (.D(sub_t), .en(1'b1), .clk(clk), .Q(sub), .clr(rst));
  and and_9 (jmp, and_7_out, d_ff_1_q);
  and and_10 (jmpn, and_8_out, d_ff_2_q);
  or or_1 (or_1_out, sub_t, add_t, ldi_t, ld_t, mv_t);
  Register #(.width(1)) register_9 (.D(or_1_out), .en(1'b1), .clk(clk), .Q(go), .clr(rst));
  and and_11 (and_11_out, mv_t, IR[4], IR[5], IR[6], IR[7]);
  Register #(.width(1)) register_10 (.D(and_11_out), .en(1'b1), .clk(clk), .Q(halt), .clr(rst));

  assign jmpData = IR[7:2];

  // Other names for the same wires on the sheet: haltTunnel[7:0] = IR; jumpTunnel[5:0] = IR[7:2]
endmodule

module cycleCounter (
  input  halt,
  input  clk,
  input  rst,
  output [15:0] cycles
);

  wire not_1_out, register_1_q;
  wire [15:0] adder_1_out;

  Register #(.width(1)) register_1 (.D(1'b1), .en(halt), .clk(clk), .Q(register_1_q), .clr(rst));
  Adder #(.width(16)) adder_1 (.a(16'h1), .b(cycles), .out(adder_1_out));  // open: cin, cout
  Register #(.width(16)) register_2 (.D(adder_1_out), .en(not_1_out), .clk(clk), .Q(cycles), .clr(rst));
  not not_1 (not_1_out, register_1_q);
endmodule
