// Logisim project Master2.circ as structural Verilog: 25 circuits, main circuit Master
module XORopt (
  input  a,
  input  b,
  output c
);

  wire nand_1_out, nor_1_out, not_1_out;

  nor nor_1 (nor_1_out, a, b);
  nand nand_1 (nand_1_out, a, b);
  not not_1 (not_1_out, nand_1_out);
  nor nor_2 (c, nor_1_out, not_1_out);
endmodule

module FA0 (
  input  A,
  input  B,
  output S,
  output Cout
);

  wire nand_1_out, nor_1_out;

  nor nor_1 (nor_1_out, A, B);
  nand nand_1 (nand_1_out, A, B);
  not not_1 (Cout, nand_1_out);
  nor nor_2 (S, nor_1_out, Cout);

  // Notes on the sheet:
  //   0
  //   0
  //   FA0
  //   14 transistors
  //   Kushaal Singh
  //   2.75
  //   1.75
endmodule

module FA1 (
  input  A,
  input  B,
  output S,
  output Cout
);

  wire nand_1_out, nor_1_out;

  nor nor_1 (nor_1_out, A, B);
  nand nand_1 (nand_1_out, A, B);
  not not_1 (Cout, nor_1_out);
  nand nand_2 (S, Cout, nand_1_out);

  // Notes on the sheet:
  //   14 transistors
  //   FA1
  //   Kushaal Singh
  //   2.75
  //   1.75
endmodule

module FAopt1 (
  input  A,
  input  B,
  input  Cin,
  output S,
  output Cout
);

  wire nand_1_out, nand_2_out, nor_1_out, nor_2_out, nor_3_out, not_1_out, not_2_out;

  nor nor_1 (nor_1_out, A, B);
  nand nand_1 (nand_1_out, A, B);
  not not_1 (not_1_out, nand_1_out);
  nor nor_2 (nor_2_out, nor_1_out, not_1_out);
  nor nor_3 (nor_3_out, nor_2_out, Cin);
  nand nand_2 (nand_2_out, nor_2_out, Cin);
  not not_2 (not_2_out, nand_2_out);
  nor nor_4 (S, nor_3_out, not_2_out);
  nand nand_3 (Cout, nand_2_out, nand_1_out);

  // Notes on the sheet:
  //   FAopt1
  //   32 transistors
  //   Kushaal Singh
  //   5.5 or Cin + 2.75
  //   4.75 or Cin + 2
endmodule

module FAopt2 (
  input  A,
  input  B,
  input  Cin,
  output S,
  output Cout
);

  wire nand_1_out, nand_2_out, nand_3_out, nand_4_out, nor_1_out, nor_2_out, nor_3_out, not_1_out, not_2_out;

  nor nor_1 (nor_1_out, A, B);
  nand nand_1 (nand_1_out, A, B);
  not not_1 (not_1_out, nand_1_out);
  nor nor_2 (nor_2_out, nor_1_out, not_1_out);
  nor nor_3 (nor_3_out, nor_2_out, Cin);
  nand nand_2 (nand_2_out, nor_2_out, Cin);
  not not_2 (not_2_out, nand_2_out);
  nand nand_3 (nand_3_out, A, Cin);
  nand nand_4 (nand_4_out, B, Cin);
  nor nor_4 (S, nor_3_out, not_2_out);
  nand nand_5 (Cout, nand_1_out, nand_3_out, nand_4_out);

  // Notes on the sheet:
  //   FAopt2
  //   42 transistors
  //   Kushaal Singh
  //   5.5 or Cin + 2.75
  //   Cin + 2.25
endmodule

module mux_2to1 (
  input  in0,
  input  S,
  input  in1,
  output Z
);

  wire nand_1_out, nand_2_out, not_1_out;

  not not_1 (not_1_out, S);
  nand nand_1 (nand_1_out, in0, not_1_out);
  nand nand_2 (nand_2_out, S, in1);
  nand nand_3 (Z, nand_1_out, nand_2_out);

  // Notes on the sheet:
  //   z = max(s+2.75, in0 + 2, in1 + 2)
  //   14 transistors
  //   mux_2to1
  //   Kushaal Singh
endmodule

module mux_4to1 (
  input  in00,
  input  in01,
  input  in10,
  input  in11,
  input  S0,
  input  S1,
  output Z
);

  wire mux_2to1_1_z, mux_2to1_3_z;

  mux_2to1 mux_2to1_1 (.in0(in00), .S(S0), .in1(in01), .Z(mux_2to1_1_z));
  mux_2to1 mux_2to1_2 (.in0(mux_2to1_1_z), .S(S1), .in1(mux_2to1_3_z), .Z(Z));
  mux_2to1 mux_2to1_3 (.in0(in10), .S(S0), .in1(in11), .Z(mux_2to1_3_z));

  // Notes on the sheet:
  //   42 transistors
  //   mux_4to1
  //   Kushaal Singh
  //   z = max(S0+4.75, S1 + 2.75, in00 + 4, in01 + 4, in10 + 4, in11 + 4)
endmodule

module mx2i (
  input  in0,
  input  S,
  input  in1,
  output Z
);

  wire transmission_1_p3, transmission_1_p4;

  // Transmission_Gate transmission_1: pin names not known; wires that end beside it: in0, S, transmission_1_p3, transmission_1_p4
  not not_1 (transmission_1_p3, S);
  // Transmission_Gate transmission_2: pin names not known; wires that end beside it: in1, transmission_1_p3, S, transmission_1_p4
  not not_2 (Z, transmission_1_p4);

  // Notes on the sheet:
  //   8 transistors
  //   mx2i
  //   Kushaal Singh
  //   z = max(S+1.75, in0 + 1, in1 + 1)
endmodule

module mx4i (
  input  in00,
  input  in01,
  input  in10,
  input  in11,
  input  S0,
  input  S1,
  output Z
);

  wire mx2i_1_z, mx2i_3_z;

  mx2i mx2i_1 (.in0(in00), .S(S0), .in1(in01), .Z(mx2i_1_z));
  mx2i mx2i_2 (.in0(mx2i_1_z), .S(S1), .in1(mx2i_3_z), .Z(Z));
  mx2i mx2i_3 (.in0(in10), .S(S0), .in1(in11), .Z(mx2i_3_z));

  // Notes on the sheet:
  //   mx4i
  //   24 transistors
  //   Kushaal Singh
  //   Z = max(S0 + 2.75, S1 + 1.75, in00+2, in01+2, in10+2, in11+2)
endmodule

module srcSel (
  input  [15:0] reg00,
  input  [15:0] reg01,
  input  [15:0] reg10,
  input  [15:0] reg11,
  input  [1:0] sel,
  output [15:0] regOut
);

  Multiplexer #(.select(2), .width(16)) multiplexer_1 (
    .in0(reg00), .in1(reg01), .in2(reg10), .in3(reg11), .out(regOut), .sel(sel));
endmodule

module regWE (
  input  [1:0] Rd,
  input  regWrite,
  output reg3WE,
  output reg2WE,
  output reg1WE,
  output reg0WE
);

  wire not_1_out, not_2_out, not_3_out, not_4_out;

  and and_1 (reg3WE, Rd[0], Rd[1], regWrite);
  not not_1 (not_1_out, Rd[0]);
  and and_2 (reg2WE, not_1_out, Rd[1], regWrite);
  not not_2 (not_2_out, Rd[1]);
  and and_3 (reg1WE, Rd[0], not_2_out, regWrite);
  not not_3 (not_3_out, Rd[0]);
  not not_4 (not_4_out, Rd[1]);
  and and_4 (reg0WE, not_3_out, not_4_out, regWrite);
endmodule

module programCounter (
  input  in_1,
  input  in_2,
  output [5:0] out_3
);

  wire adder_1_cout;
  wire [5:0] adder_1_out;

  Adder #(.width(6)) adder_1 (.a(6'b000001), .b(out_3), .out(adder_1_out), .cin(adder_1_cout), .cout(adder_1_cout));
  Register #(.width(6)) register_1 (.D(adder_1_out), .en(1'b1), .clk(in_1), .Q(out_3), .clr(in_2));
  // also tied to GND on the sheet: adder_1_cout
endmodule

module rippleAdder4BitCin (
  input  Cin,
  input  [3:0] a,
  input  [3:0] b,
  output [3:0] out_4,
  output out_5
);

  wire faopt1_2_cout, faopt1_3_cout, faopt2_1_cout;

  FAopt1 faopt1_1 (.A(a[3]), .B(b[3]), .Cin(faopt1_2_cout), .S(out_4[3]), .Cout(out_5));
  FAopt1 faopt1_2 (.A(a[2]), .B(b[2]), .Cin(faopt2_1_cout), .S(out_4[2]), .Cout(faopt1_2_cout));
  FAopt2 faopt2_1 (.A(a[1]), .B(b[1]), .Cin(faopt1_3_cout), .S(out_4[1]), .Cout(faopt2_1_cout));
  FAopt1 faopt1_3 (.A(a[0]), .B(b[0]), .Cin(Cin), .S(out_4[0]), .Cout(faopt1_3_cout));

  // Notes on the sheet:
  //   Kushaal Singh
endmodule

module rippleAdder4Bit0 (
  input  [3:0] a,
  input  [3:0] b,
  output [3:0] _8_75,
  output _8
);

  wire fa0_1_cout, faopt1_2_cout, faopt2_1_cout;

  FAopt1 faopt1_1 (.A(a[3]), .B(b[3]), .Cin(faopt1_2_cout), .S(_8_75[3]), .Cout(_8));
  FAopt1 faopt1_2 (.A(a[2]), .B(b[2]), .Cin(faopt2_1_cout), .S(_8_75[2]), .Cout(faopt1_2_cout));
  FAopt2 faopt2_1 (.A(a[1]), .B(b[1]), .Cin(fa0_1_cout), .S(_8_75[1]), .Cout(faopt2_1_cout));
  FA0 fa0_1 (.A(a[0]), .B(b[0]), .S(_8_75[0]), .Cout(fa0_1_cout));

  // Notes on the sheet:
  //   0
  //   0
  //   8
  //   8.75
  //   6
  //   4
  //   6.75
  //   1.75
  //   5.5
  //   2.75
  //   Kushaal Singh
  //   4 bit ripple adder
  //   120 transistors
endmodule

module rippleAdder4Bit1 (
  input  [3:0] a,
  input  [3:0] b,
  output [3:0] _8_75,
  output _8
);

  wire fa1_1_cout, faopt1_2_cout, faopt2_1_cout;

  FAopt1 faopt1_1 (.A(a[3]), .B(b[3]), .Cin(faopt1_2_cout), .S(_8_75[3]), .Cout(_8));
  FAopt1 faopt1_2 (.A(a[2]), .B(b[2]), .Cin(faopt2_1_cout), .S(_8_75[2]), .Cout(faopt1_2_cout));
  FAopt2 faopt2_1 (.A(a[1]), .B(b[1]), .Cin(fa1_1_cout), .S(_8_75[1]), .Cout(faopt2_1_cout));
  FA1 fa1_1 (.A(a[0]), .B(b[0]), .S(_8_75[0]), .Cout(fa1_1_cout));

  // Notes on the sheet:
  //   0
  //   0
  //   8
  //   8.75
  //   6
  //   4
  //   6.75
  //   1.75
  //   5.5
  //   2.75
  //   Kushaal Singh
  //   4 bit ripple adder
  //   120 transistors
endmodule

module rippleAdder8Bit (
  input  [7:0] _0,
  input  [7:0] _0_2,
  output [7:0] _16_75,
  output _16
);

  wire fa0_1_cout, faopt1_2_cout, faopt1_3_cout, faopt1_4_cout, faopt1_5_cout, faopt1_6_cout, faopt2_1_cout;

  FAopt1 faopt1_1 (.A(_0[7]), .B(_0_2[7]), .Cin(faopt1_2_cout), .S(_16_75[7]), .Cout(_16));
  FAopt1 faopt1_2 (.A(_0[6]), .B(_0_2[6]), .Cin(faopt1_3_cout), .S(_16_75[6]), .Cout(faopt1_2_cout));
  FAopt1 faopt1_3 (.A(_0[5]), .B(_0_2[5]), .Cin(faopt1_4_cout), .S(_16_75[5]), .Cout(faopt1_3_cout));
  FAopt1 faopt1_4 (.A(_0[4]), .B(_0_2[4]), .Cin(faopt1_5_cout), .S(_16_75[4]), .Cout(faopt1_4_cout));
  FAopt1 faopt1_5 (.A(_0[3]), .B(_0_2[3]), .Cin(faopt1_6_cout), .S(_16_75[3]), .Cout(faopt1_5_cout));
  FAopt1 faopt1_6 (.A(_0[2]), .B(_0_2[2]), .Cin(faopt2_1_cout), .S(_16_75[2]), .Cout(faopt1_6_cout));
  FAopt2 faopt2_1 (.A(_0[1]), .B(_0_2[1]), .Cin(fa0_1_cout), .S(_16_75[1]), .Cout(faopt2_1_cout));
  FA0 fa0_1 (.A(_0[0]), .B(_0_2[0]), .S(_16_75[0]), .Cout(fa0_1_cout));

  // Notes on the sheet:
  //   16
  //   14
  //   16.75
  //   12
  //   14.75
  //   12.75
  //   10
  //   8
  //   10.75
  //   6
  //   8.75
  //   4
  //   6.75
  //   5.5
  //   1.75
  //   2.75
  //   Kushaal Singh
  //   8 bit ripple adder
  //   248 transistors
endmodule

module carrySelectAdder8BitCin (
  input  in_1,
  input  [7:0] in_2,
  input  [7:0] in_3,
  output [7:0] out_4,
  output _10_5
);

  wire mx2i_1_z, mx2i_2_z, mx2i_3_z, mx2i_4_z, mx2i_5_z, rippleadder4bit0_1__8, rippleadder4bit1_1__8,
       rippleadder4bitcin_1_out_5;
  wire [3:0] rippleadder4bit0_1__8_75, rippleadder4bit1_1__8_75;

  mx2i mx2i_1 (
    .in0(rippleadder4bit0_1__8_75[0]), .S(rippleadder4bitcin_1_out_5), .in1(rippleadder4bit1_1__8_75[0]),
    .Z(mx2i_1_z));
  mx2i mx2i_2 (
    .in0(rippleadder4bit0_1__8_75[1]), .S(rippleadder4bitcin_1_out_5), .in1(rippleadder4bit1_1__8_75[1]),
    .Z(mx2i_2_z));
  mx2i mx2i_3 (
    .in0(rippleadder4bit0_1__8_75[2]), .S(rippleadder4bitcin_1_out_5), .in1(rippleadder4bit1_1__8_75[2]),
    .Z(mx2i_3_z));
  mx2i mx2i_4 (
    .in0(rippleadder4bit0_1__8_75[3]), .S(rippleadder4bitcin_1_out_5), .in1(rippleadder4bit1_1__8_75[3]),
    .Z(mx2i_4_z));
  mx2i mx2i_5 (.in0(rippleadder4bit0_1__8), .S(rippleadder4bitcin_1_out_5), .in1(rippleadder4bit1_1__8), .Z(mx2i_5_z));
  rippleAdder4Bit1 rippleadder4bit1_1 (
    .a(in_2[7:4]), .b(in_3[7:4]), ._8_75(rippleadder4bit1_1__8_75), ._8(rippleadder4bit1_1__8));
  not not_1 (out_4[4], mx2i_1_z);
  not not_2 (out_4[5], mx2i_2_z);
  not not_3 (out_4[6], mx2i_3_z);
  not not_4 (out_4[7], mx2i_4_z);
  not not_5 (_10_5, mx2i_5_z);
  rippleAdder4Bit0 rippleadder4bit0_1 (
    .a(in_2[7:4]), .b(in_3[7:4]), ._8_75(rippleadder4bit0_1__8_75), ._8(rippleadder4bit0_1__8));
  rippleAdder4BitCin rippleadder4bitcin_1 (
    .Cin(in_1), .a(in_3[3:0]), .b(in_2[3:0]), .out_4(out_4[3:0]), .out_5(rippleadder4bitcin_1_out_5));

  // Notes on the sheet:
  //   8
  //   8.75
  //   8
  //   8.75
  //   8
  //   8.75
  //   Kushaal Singh
  //   10.5
endmodule

module carrySelectAdder8Bit (
  input  [7:0] _0,
  input  [7:0] _0_2,
  output [7:0] out_3,
  output _10_5
);

  wire mx2i_1_z, mx2i_2_z, mx2i_3_z, mx2i_4_z, mx2i_5_z, rippleadder4bit0_1__8, rippleadder4bit0_2__8,
       rippleadder4bit1_1__8;
  wire [3:0] rippleadder4bit0_1__8_75, rippleadder4bit1_1__8_75;

  mx2i mx2i_1 (
    .in0(rippleadder4bit0_1__8_75[0]), .S(rippleadder4bit0_2__8), .in1(rippleadder4bit1_1__8_75[0]),
    .Z(mx2i_1_z));
  mx2i mx2i_2 (
    .in0(rippleadder4bit0_1__8_75[1]), .S(rippleadder4bit0_2__8), .in1(rippleadder4bit1_1__8_75[1]),
    .Z(mx2i_2_z));
  mx2i mx2i_3 (
    .in0(rippleadder4bit0_1__8_75[2]), .S(rippleadder4bit0_2__8), .in1(rippleadder4bit1_1__8_75[2]),
    .Z(mx2i_3_z));
  mx2i mx2i_4 (
    .in0(rippleadder4bit0_1__8_75[3]), .S(rippleadder4bit0_2__8), .in1(rippleadder4bit1_1__8_75[3]),
    .Z(mx2i_4_z));
  mx2i mx2i_5 (.in0(rippleadder4bit0_1__8), .S(rippleadder4bit0_2__8), .in1(rippleadder4bit1_1__8), .Z(mx2i_5_z));
  rippleAdder4Bit1 rippleadder4bit1_1 (
    .a(_0[7:4]), .b(_0_2[7:4]), ._8_75(rippleadder4bit1_1__8_75), ._8(rippleadder4bit1_1__8));
  not not_1 (out_3[4], mx2i_1_z);
  not not_2 (out_3[5], mx2i_2_z);
  not not_3 (out_3[6], mx2i_3_z);
  not not_4 (out_3[7], mx2i_4_z);
  not not_5 (_10_5, mx2i_5_z);
  rippleAdder4Bit0 rippleadder4bit0_1 (
    .a(_0[7:4]), .b(_0_2[7:4]), ._8_75(rippleadder4bit0_1__8_75), ._8(rippleadder4bit0_1__8));
  rippleAdder4Bit0 rippleadder4bit0_2 (.a(_0[3:0]), .b(_0_2[3:0]), ._8_75(out_3[3:0]), ._8(rippleadder4bit0_2__8));

  // Notes on the sheet:
  //   8
  //   8.75
  //   8
  //   8.75
  //   8
  //   8.75
  //   370 transistors
  //   Kushaal Singh
  //   8 bit carry select adder
  //   10.5
endmodule

module carrySelectAdder16BitCin (
  input  Cin,
  input  [15:0] A,
  input  [15:0] B,
  output out_4,
  output [15:0] out_5
);

  wire carryselectadder8bit_1__10_5, carryselectadder8bitcin_1__10_5, mx2i_1_z, mx2i_2_z, mx2i_3_z, mx2i_4_z,
       mx2i_5_z, mx2i_6_z, mx2i_7_z, mx2i_8_z, mx2i_9_z, mx2i_10_z, mx2i_11_z, mx2i_12_z, mx2i_13_z,
       mx2i_14_z, not_1_out, not_2_out, not_3_out, not_4_out, not_5_out, rippleadder4bit0_1__8,
       rippleadder4bit1_1__8, rippleadder4bit1_2__8;
  wire [3:0] rippleadder4bit0_1__8_75, rippleadder4bit1_1__8_75, rippleadder4bit1_2__8_75;
  wire [7:0] carryselectadder8bit_1_out_3;

  mx2i mx2i_1 (
    .in0(rippleadder4bit0_1__8_75[0]), .S(rippleadder4bit1_2__8), .in1(rippleadder4bit1_1__8_75[0]),
    .Z(mx2i_1_z));
  mx2i mx2i_2 (
    .in0(rippleadder4bit0_1__8_75[1]), .S(rippleadder4bit1_2__8), .in1(rippleadder4bit1_1__8_75[1]),
    .Z(mx2i_2_z));
  mx2i mx2i_3 (
    .in0(rippleadder4bit0_1__8_75[2]), .S(rippleadder4bit1_2__8), .in1(rippleadder4bit1_1__8_75[2]),
    .Z(mx2i_3_z));
  mx2i mx2i_4 (
    .in0(rippleadder4bit0_1__8_75[3]), .S(rippleadder4bit1_2__8), .in1(rippleadder4bit1_1__8_75[3]),
    .Z(mx2i_4_z));
  mx2i mx2i_5 (.in0(rippleadder4bit0_1__8), .S(rippleadder4bit1_2__8), .in1(rippleadder4bit1_1__8), .Z(mx2i_5_z));
  rippleAdder4Bit1 rippleadder4bit1_1 (
    .a(A[15:12]), .b(B[15:12]), ._8_75(rippleadder4bit1_1__8_75), ._8(rippleadder4bit1_1__8));
  not not_1 (not_1_out, mx2i_1_z);
  not not_2 (not_2_out, mx2i_2_z);
  not not_3 (not_3_out, mx2i_3_z);
  not not_4 (not_4_out, mx2i_4_z);
  not not_5 (not_5_out, mx2i_5_z);
  rippleAdder4Bit0 rippleadder4bit0_1 (
    .a(A[15:12]), .b(B[15:12]), ._8_75(rippleadder4bit0_1__8_75), ._8(rippleadder4bit0_1__8));
  rippleAdder4Bit1 rippleadder4bit1_2 (
    .a(A[11:8]), .b(B[11:8]), ._8_75(rippleadder4bit1_2__8_75), ._8(rippleadder4bit1_2__8));
  carrySelectAdder8Bit carryselectadder8bit_1 (
    ._0(A[15:8]), ._0_2(B[15:8]), .out_3(carryselectadder8bit_1_out_3), ._10_5(carryselectadder8bit_1__10_5));
  carrySelectAdder8BitCin carryselectadder8bitcin_1 (
    .in_1(Cin), .in_2(A[7:0]), .in_3(B[7:0]), .out_4(out_5[7:0]), ._10_5(carryselectadder8bitcin_1__10_5));
  mx2i mx2i_6 (
    .in0(carryselectadder8bit_1_out_3[0]), .S(carryselectadder8bitcin_1__10_5),
    .in1(rippleadder4bit1_2__8_75[0]), .Z(mx2i_6_z));
  mx2i mx2i_7 (
    .in0(carryselectadder8bit_1_out_3[1]), .S(carryselectadder8bitcin_1__10_5),
    .in1(rippleadder4bit1_2__8_75[1]), .Z(mx2i_7_z));
  mx2i mx2i_8 (
    .in0(carryselectadder8bit_1_out_3[2]), .S(carryselectadder8bitcin_1__10_5),
    .in1(rippleadder4bit1_2__8_75[2]), .Z(mx2i_8_z));
  mx2i mx2i_9 (
    .in0(carryselectadder8bit_1_out_3[3]), .S(carryselectadder8bitcin_1__10_5),
    .in1(rippleadder4bit1_2__8_75[3]), .Z(mx2i_9_z));
  mx2i mx2i_10 (
    .in0(carryselectadder8bit_1_out_3[4]), .S(carryselectadder8bitcin_1__10_5), .in1(not_1_out), .Z(mx2i_10_z));
  mx2i mx2i_11 (
    .in0(carryselectadder8bit_1_out_3[5]), .S(carryselectadder8bitcin_1__10_5), .in1(not_2_out), .Z(mx2i_11_z));
  mx2i mx2i_12 (
    .in0(carryselectadder8bit_1_out_3[6]), .S(carryselectadder8bitcin_1__10_5), .in1(not_3_out), .Z(mx2i_12_z));
  mx2i mx2i_13 (
    .in0(carryselectadder8bit_1_out_3[7]), .S(carryselectadder8bitcin_1__10_5), .in1(not_4_out), .Z(mx2i_13_z));
  mx2i mx2i_14 (
    .in0(carryselectadder8bit_1__10_5), .S(carryselectadder8bitcin_1__10_5), .in1(not_5_out), .Z(mx2i_14_z));
  not not_6 (out_5[8], mx2i_6_z);
  not not_7 (out_5[9], mx2i_7_z);
  not not_8 (out_5[10], mx2i_8_z);
  not not_9 (out_5[11], mx2i_9_z);
  not not_10 (out_5[12], mx2i_10_z);
  not not_11 (out_5[13], mx2i_11_z);
  not not_12 (out_5[14], mx2i_12_z);
  not not_13 (out_5[15], mx2i_13_z);
  not not_14 (out_4, mx2i_14_z);

  // Notes on the sheet:
  //   0
  //   0
  //   Kushaal Singh
endmodule

module carrySelectAdder16Bit (
  input  [15:0] in_1,
  input  [15:0] _0,
  output _13,
  output [15:0] out_4
);

  wire carryselectadder8bit_1__10_5, carryselectadder8bit_2__10_5, mx2i_1_z, mx2i_2_z, mx2i_3_z, mx2i_4_z,
       mx2i_5_z, mx2i_6_z, mx2i_7_z, mx2i_8_z, mx2i_9_z, mx2i_10_z, mx2i_11_z, mx2i_12_z, mx2i_13_z,
       mx2i_14_z, not_1_out, not_2_out, not_3_out, not_4_out, not_5_out, rippleadder4bit0_1__8,
       rippleadder4bit1_1__8, rippleadder4bit1_2__8;
  wire [3:0] rippleadder4bit0_1__8_75, rippleadder4bit1_1__8_75, rippleadder4bit1_2__8_75;
  wire [7:0] carryselectadder8bit_1_out_3;

  mx2i mx2i_1 (
    .in0(rippleadder4bit0_1__8_75[0]), .S(rippleadder4bit1_2__8), .in1(rippleadder4bit1_1__8_75[0]),
    .Z(mx2i_1_z));
  mx2i mx2i_2 (
    .in0(rippleadder4bit0_1__8_75[1]), .S(rippleadder4bit1_2__8), .in1(rippleadder4bit1_1__8_75[1]),
    .Z(mx2i_2_z));
  mx2i mx2i_3 (
    .in0(rippleadder4bit0_1__8_75[2]), .S(rippleadder4bit1_2__8), .in1(rippleadder4bit1_1__8_75[2]),
    .Z(mx2i_3_z));
  mx2i mx2i_4 (
    .in0(rippleadder4bit0_1__8_75[3]), .S(rippleadder4bit1_2__8), .in1(rippleadder4bit1_1__8_75[3]),
    .Z(mx2i_4_z));
  mx2i mx2i_5 (.in0(rippleadder4bit0_1__8), .S(rippleadder4bit1_2__8), .in1(rippleadder4bit1_1__8), .Z(mx2i_5_z));
  rippleAdder4Bit1 rippleadder4bit1_1 (
    .a(in_1[15:12]), .b(_0[15:12]), ._8_75(rippleadder4bit1_1__8_75), ._8(rippleadder4bit1_1__8));
  not not_1 (not_1_out, mx2i_1_z);
  not not_2 (not_2_out, mx2i_2_z);
  not not_3 (not_3_out, mx2i_3_z);
  not not_4 (not_4_out, mx2i_4_z);
  not not_5 (not_5_out, mx2i_5_z);
  rippleAdder4Bit0 rippleadder4bit0_1 (
    .a(in_1[15:12]), .b(_0[15:12]), ._8_75(rippleadder4bit0_1__8_75), ._8(rippleadder4bit0_1__8));
  rippleAdder4Bit1 rippleadder4bit1_2 (
    .a(in_1[11:8]), .b(_0[11:8]), ._8_75(rippleadder4bit1_2__8_75), ._8(rippleadder4bit1_2__8));
  carrySelectAdder8Bit carryselectadder8bit_1 (
    ._0(in_1[15:8]), ._0_2(_0[15:8]), .out_3(carryselectadder8bit_1_out_3),
    ._10_5(carryselectadder8bit_1__10_5));
  carrySelectAdder8Bit carryselectadder8bit_2 (
    ._0(in_1[7:0]), ._0_2(_0[7:0]), .out_3(out_4[7:0]), ._10_5(carryselectadder8bit_2__10_5));
  not not_6 (out_4[8], mx2i_6_z);
  mx2i mx2i_6 (
    .in0(carryselectadder8bit_1_out_3[0]), .S(carryselectadder8bit_2__10_5),
    .in1(rippleadder4bit1_2__8_75[0]), .Z(mx2i_6_z));
  not not_7 (out_4[9], mx2i_7_z);
  mx2i mx2i_7 (
    .in0(carryselectadder8bit_1_out_3[1]), .S(carryselectadder8bit_2__10_5),
    .in1(rippleadder4bit1_2__8_75[1]), .Z(mx2i_7_z));
  not not_8 (out_4[10], mx2i_8_z);
  mx2i mx2i_8 (
    .in0(carryselectadder8bit_1_out_3[2]), .S(carryselectadder8bit_2__10_5),
    .in1(rippleadder4bit1_2__8_75[2]), .Z(mx2i_8_z));
  not not_9 (out_4[11], mx2i_9_z);
  mx2i mx2i_9 (
    .in0(carryselectadder8bit_1_out_3[3]), .S(carryselectadder8bit_2__10_5),
    .in1(rippleadder4bit1_2__8_75[3]), .Z(mx2i_9_z));
  not not_10 (out_4[12], mx2i_10_z);
  mx2i mx2i_10 (
    .in0(carryselectadder8bit_1_out_3[4]), .S(carryselectadder8bit_2__10_5), .in1(not_1_out), .Z(mx2i_10_z));
  not not_11 (out_4[13], mx2i_11_z);
  mx2i mx2i_11 (
    .in0(carryselectadder8bit_1_out_3[5]), .S(carryselectadder8bit_2__10_5), .in1(not_2_out), .Z(mx2i_11_z));
  not not_12 (out_4[14], mx2i_12_z);
  mx2i mx2i_12 (
    .in0(carryselectadder8bit_1_out_3[6]), .S(carryselectadder8bit_2__10_5), .in1(not_3_out), .Z(mx2i_12_z));
  not not_13 (out_4[15], mx2i_13_z);
  mx2i mx2i_13 (
    .in0(carryselectadder8bit_1_out_3[7]), .S(carryselectadder8bit_2__10_5), .in1(not_4_out), .Z(mx2i_13_z));
  not not_14 (_13, mx2i_14_z);
  mx2i mx2i_14 (.in0(carryselectadder8bit_1__10_5), .S(carryselectadder8bit_2__10_5), .in1(not_5_out), .Z(mx2i_14_z));

  // Notes on the sheet:
  //   0
  //   13
  //   1182 Transistors
  //   Kushaal Singh
  //   16 bit select adder
endmodule

module carryLookAhead (
  input  c0,
  input  p0,
  input  p1,
  input  p2,
  input  p3,
  input  g0,
  input  g1,
  input  g2,
  input  g3,
  output out_10
);

  wire and_1_out, and_2_out, nand_1_out, nor_1_out, nor_2_out, nor_3_out, nor_4_out, not_1_out, not_2_out,
       not_3_out;

  not not_1 (not_1_out, c0);
  not not_2 (not_2_out, p0);
  nand nand_1 (nand_1_out, p1, p2, p3);
  not not_3 (not_3_out, g0);
  and and_1 (and_1_out, p3, p2, g1);
  and and_2 (and_2_out, p3, g2);
  nor nor_1 (nor_1_out, not_1_out, not_2_out, nand_1_out);
  nor nor_2 (nor_2_out, nand_1_out, not_3_out);
  nor nor_3 (nor_3_out, nor_1_out, nor_2_out);
  nor nor_4 (nor_4_out, and_1_out, and_2_out, g3);
  nand nand_2 (out_10, nor_3_out, nor_4_out);
endmodule

module addersubtractor (
  input  op,
  input  [15:0] A,
  input  [15:0] B,
  output [15:0] S,
  output overflow
);

  wire carryselectadder16bitcin_1_out_4, multiplexer_2_out, multiplexer_3_out, not_2_out, not_3_out,
       not_4_out;
  wire [15:0] multiplexer_1_out, not_1_out;

  Multiplexer #(.width(16)) multiplexer_1 (.in0(B), .in1(not_1_out), .out(multiplexer_1_out), .sel(op));
  assign not_1_out = ~B;  // NOT_Gate not_1, 16 bits wide
  carrySelectAdder16BitCin carryselectadder16bitcin_1 (
    .Cin(op), .A(multiplexer_1_out), .B(A), .out_4(carryselectadder16bitcin_1_out_4), .out_5(S));
  Multiplexer multiplexer_2 (.in0(A[15]), .in1(not_2_out), .out(multiplexer_2_out), .sel(multiplexer_1_out[15]));
  not not_2 (not_2_out, A[15]);
  not not_3 (not_3_out, S[15]);
  not not_4 (not_4_out, multiplexer_2_out);
  Multiplexer multiplexer_3 (
    .in0(S[15]), .in1(not_3_out), .out(multiplexer_3_out), .sel(carryselectadder16bitcin_1_out_4));
  and and_1 (overflow, multiplexer_3_out, not_4_out);
endmodule

module decoderLALU (
  input  [7:0] IR,
  input  clk,
  input  rst,
  output ld,
  output ldi,
  output Add,
  output Sub,
  output [1:0] Rd,
  output [1:0] Rs
);

  wire and_1_out, and_2_out, and_3_out, and_4_out, not_1_out, not_2_out, not_3_out, not_4_out;

  not not_1 (not_1_out, IR[0]);
  not not_2 (not_2_out, IR[1]);
  not not_3 (not_3_out, IR[2]);
  not not_4 (not_4_out, IR[3]);
  and and_1 (and_1_out, IR[3], IR[2], IR[1], IR[0]);
  and and_2 (and_2_out, IR[3], IR[2], IR[1], not_1_out);
  and and_3 (and_3_out, not_4_out, not_3_out, IR[1], not_1_out);
  and and_4 (and_4_out, not_4_out, not_3_out, IR[1], IR[0]);
  Register #(.width(1)) register_1 (.D(and_1_out), .en(1'b1), .clk(clk), .Q(ld), .clr(rst));
  Register #(.width(1)) register_2 (.D(and_2_out), .en(1'b1), .clk(clk), .Q(ldi), .clr(rst));
  Register #(.width(1)) register_3 (.D(and_3_out), .en(1'b1), .clk(clk), .Q(Add), .clr(rst));
  Register #(.width(1)) register_4 (.D(and_4_out), .en(1'b1), .clk(clk), .Q(Sub), .clr(rst));
  Register #(.width(2)) register_5 (.D(IR[7:6]), .en(1'b1), .clk(clk), .Q(Rd), .clr(rst));
  Register #(.width(2)) register_6 (.D(IR[5:4]), .en(1'b1), .clk(clk), .Q(Rs), .clr(rst));
endmodule

module Master (
  input  rst
);

  wire addersubtractor_1_overflow, and_1_out, clk_out, decoderlalu_1_add, decoderlalu_1_ld,
       decoderlalu_1_ldi, decoderlalu_1_sub, register_1_q, register_2_q, register_3_q, regwe_1_reg0we,
       regwe_1_reg1we, regwe_1_reg2we, regwe_1_reg3we;
  wire [1:0] decoderlalu_1_rd, decoderlalu_1_rs;
  wire [3:0] load_q, load_q_2, R0_q, R0_q_2, R0_q_3, R0_q_4, R1_q, R1_q_2, R1_q_3, R1_q_4, R2_q, R2_q_2,
       R2_q_3, R2_q_4, R3_q, R3_q_2, R3_q_3, R3_q_4, srcsel_2_regout;
  wire [5:0] programcounter_1_out_3;
  wire [7:0] decode_q, execute_q, ram_1_dout;
  wire [15:0] addersubtractor_1_s, multiplexer_1_out, multiplexer_2_out, multiplexer_3_out,
       multiplexer_4_out, ram_2_dout, srcsel_1_regout;
  wire [15:4] srcsel_2_regout_2;

  Clock clk (.out(clk_out));
  RAM #(.addrWidth(6), .asyncread("true"), .trigger("falling")) ram_1 (
    .addr(programcounter_1_out_3), .we(1'b0), .oe(1'b1), .clk(clk_out), .dout(ram_1_dout));  // open: din
  RAM #(.addrWidth(4), .asyncread("true"), .dataWidth(16), .trigger("falling")) ram_2 (
    .addr(srcsel_2_regout), .we(1'b0), .oe(1'b1), .clk(clk_out), .dout(ram_2_dout));  // open: din
  programCounter programcounter_1 (.in_1(clk_out), .in_2(rst), .out_3(programcounter_1_out_3));
  Register load (.D(ram_1_dout), .en(1'b1), .clk(clk_out), .Q({load_q_2, load_q}), .clr(rst));
  Register #(.width(1)) register_1 (.D(1'b1), .en(1'b1), .clk(clk_out), .Q(register_1_q), .clr(rst));
  Register #(.width(1)) register_2 (.D(register_1_q), .en(1'b1), .clk(clk_out), .Q(register_2_q), .clr(rst));
  decoderLALU decoderlalu_1 (
    .IR({load_q_2, load_q}), .clk(clk_out), .rst(rst), .ld(decoderlalu_1_ld), .ldi(decoderlalu_1_ldi),
    .Add(decoderlalu_1_add), .Sub(decoderlalu_1_sub), .Rd(decoderlalu_1_rd), .Rs(decoderlalu_1_rs));
  Hex_Digit_Display hex_digit_display_1 (.value(load_q_2));  // open: dp
  Hex_Digit_Display hex_digit_display_2 (.value(load_q));  // open: dp
  Register decode (.D({load_q_2, load_q}), .en(1'b1), .clk(clk_out), .Q(decode_q), .clr(rst));
  srcSel srcsel_1 (
    .sel(decoderlalu_1_rd), .reg00({R0_q_4, R0_q_3, R0_q_2, R0_q}), .reg01({R1_q_4, R1_q_3, R1_q_2, R1_q}),
    .reg10({R2_q_4, R2_q_3, R2_q_2, R2_q}), .reg11({R3_q_4, R3_q_3, R3_q_2, R3_q}), .regOut(srcsel_1_regout));
  srcSel srcsel_2 (
    .sel(decoderlalu_1_rs), .reg00({R0_q_4, R0_q_3, R0_q_2, R0_q}), .reg01({R1_q_4, R1_q_3, R1_q_2, R1_q}),
    .reg10({R2_q_4, R2_q_3, R2_q_2, R2_q}), .reg11({R3_q_4, R3_q_3, R3_q_2, R3_q}),
    .regOut({srcsel_2_regout_2, srcsel_2_regout}));
  Hex_Digit_Display hex_digit_display_3 (.value(decode_q[7:4]));  // open: dp
  Multiplexer #(.width(16)) multiplexer_1 (
    .in0({16{1'b0}}), .in1(addersubtractor_1_s), .out(multiplexer_1_out), .sel(decoderlalu_1_sub));
  Multiplexer #(.width(16)) multiplexer_2 (
    .in0(multiplexer_1_out), .in1(addersubtractor_1_s), .out(multiplexer_2_out), .sel(decoderlalu_1_add));
  Hex_Digit_Display hex_digit_display_4 (.value(decode_q[3:0]));  // open: dp
  Register execute (.D(decode_q), .en(1'b1), .clk(clk_out), .Q(execute_q), .clr(rst));
  Multiplexer #(.width(16)) multiplexer_3 (
    .in0(multiplexer_2_out), .in1({{14{1'b0}}, decoderlalu_1_rs}), .out(multiplexer_3_out),
    .sel(decoderlalu_1_ldi));
  Multiplexer #(.width(16)) multiplexer_4 (
    .in0(multiplexer_3_out), .in1(ram_2_dout), .out(multiplexer_4_out), .sel(decoderlalu_1_ld));
  Hex_Digit_Display hex_digit_display_5 (.value(execute_q[7:4]));  // open: dp
  Hex_Digit_Display hex_digit_display_6 (.value(execute_q[3:0]));  // open: dp
  regWE regwe_1 (
    .regWrite(register_2_q), .Rd(decoderlalu_1_rd), .reg3WE(regwe_1_reg3we), .reg2WE(regwe_1_reg2we),
    .reg1WE(regwe_1_reg1we), .reg0WE(regwe_1_reg0we));
  addersubtractor addersubtractor_1 (
    .op(decoderlalu_1_sub), .B({srcsel_2_regout_2, srcsel_2_regout}), .A(srcsel_1_regout),
    .S(addersubtractor_1_s), .overflow(addersubtractor_1_overflow));
  Hex_Digit_Display hex_digit_display_7 (.value(multiplexer_4_out[15:12]));  // open: dp
  and and_1 (and_1_out, addersubtractor_1_overflow, register_2_q);
  Hex_Digit_Display hex_digit_display_8 (.value(multiplexer_4_out[11:8]));  // open: dp
  Hex_Digit_Display hex_digit_display_9 (.value(multiplexer_4_out[7:4]));  // open: dp
  Register #(.width(16)) R0 (
    .D(multiplexer_4_out), .en(regwe_1_reg0we), .clk(clk_out), .Q({R0_q_4, R0_q_3, R0_q_2, R0_q}), .clr(rst));
  Register #(.width(16)) R1 (
    .D(multiplexer_4_out), .en(regwe_1_reg1we), .clk(clk_out), .Q({R1_q_4, R1_q_3, R1_q_2, R1_q}), .clr(rst));
  Register #(.width(16)) R2 (
    .D(multiplexer_4_out), .en(regwe_1_reg2we), .clk(clk_out), .Q({R2_q_4, R2_q_3, R2_q_2, R2_q}), .clr(rst));
  Register #(.width(16)) R3 (
    .D(multiplexer_4_out), .en(regwe_1_reg3we), .clk(clk_out), .Q({R3_q_4, R3_q_3, R3_q_2, R3_q}), .clr(rst));
  Register #(.width(1)) register_3 (.D(1'b1), .en(and_1_out), .clk(clk_out), .Q(register_3_q), .clr(rst));
  Hex_Digit_Display hex_digit_display_10 (.value(multiplexer_4_out[3:0]));  // open: dp
  LED led_1 (.in(register_3_q));
  Hex_Digit_Display hex_digit_display_11 (.value(R0_q_4));  // open: dp
  Hex_Digit_Display hex_digit_display_12 (.value(R0_q_3));  // open: dp
  Hex_Digit_Display hex_digit_display_13 (.value(R1_q_4));  // open: dp
  Hex_Digit_Display hex_digit_display_14 (.value(R1_q_3));  // open: dp
  Hex_Digit_Display hex_digit_display_15 (.value(R2_q_4));  // open: dp
  Hex_Digit_Display hex_digit_display_16 (.value(R2_q_3));  // open: dp
  Hex_Digit_Display hex_digit_display_17 (.value(R3_q_4));  // open: dp
  Hex_Digit_Display hex_digit_display_18 (.value(R3_q_3));  // open: dp
  Hex_Digit_Display hex_digit_display_19 (.value(R0_q_2));  // open: dp
  Hex_Digit_Display hex_digit_display_20 (.value(R0_q));  // open: dp
  Hex_Digit_Display hex_digit_display_21 (.value(R1_q_2));  // open: dp
  Hex_Digit_Display hex_digit_display_22 (.value(R1_q));  // open: dp
  Hex_Digit_Display hex_digit_display_23 (.value(R2_q_2));  // open: dp
  Hex_Digit_Display hex_digit_display_24 (.value(R2_q));  // open: dp
  Hex_Digit_Display hex_digit_display_25 (.value(R3_q_2));  // open: dp
  Hex_Digit_Display hex_digit_display_26 (.value(R3_q));  // open: dp
endmodule

module betterMaster (
  input  rst,
  input  [1:0] Aselect,
  input  [1:0] Bselect,
  input  Subtract
);

  wire and_1_out, and_2_out, and_3_out, and_4_out, and_5_out, clk_out, multiplexer_4_out, multiplexer_5_out,
       mx2i_1_z, mx2i_2_z, mx2i_3_z, mx2i_4_z, mx2i_5_z, mx2i_6_z, mx2i_7_z, mx2i_8_z, mx2i_9_z, nand_1_out,
       nand_2_out, nand_3_out, nand_4_out, nand_5_out, nand_6_out, nand_7_out, nand_8_out, nand_9_out,
       nand_10_out, nand_11_out, nand_12_out, nand_13_out, nand_14_out, nand_15_out, nand_16_out,
       nand_17_out, nand_18_out, nand_19_out, nand_20_out, nand_21_out, nand_22_out, nand_23_out,
       nand_24_out, nand_25_out, nand_26_out, nand_27_out, nand_28_out, nand_29_out, nand_30_out,
       nand_31_out, nand_32_out, nand_33_out, nand_34_out, nand_35_out, nand_36_out, nand_37_out,
       nand_38_out, nand_39_out, nand_40_out, nand_41_out, nand_42_out, nand_43_out, nand_44_out,
       nand_45_out, nand_46_out, nand_47_out, nand_48_out, nand_49_out, nand_50_out, nand_52_out,
       nand_53_out, nand_54_out, nand_55_out, nand_56_out, nand_57_out, nand_58_out, nand_59_out,
       nand_60_out, nand_61_out, nand_62_out, nand_63_out, nand_64_out, nand_65_out, nand_66_out,
       nand_67_out, nand_68_out, nand_69_out, nand_70_out, nand_71_out, nand_72_out, nand_73_out,
       nand_74_out, nand_75_out, nand_76_out, nand_77_out, nand_78_out, nand_79_out, nand_80_out,
       nand_81_out, nand_82_out, nand_83_out, nand_84_out, nand_85_out, nand_86_out, nand_87_out,
       nand_88_out, nand_90_out, nand_91_out, nand_92_out, nand_93_out, nand_94_out, nand_95_out,
       nand_96_out, nand_97_out, nand_99_out, nor_1_out, nor_2_out, nor_3_out, nor_4_out, nor_6_out,
       nor_7_out, nor_8_out, nor_9_out, nor_11_out, nor_12_out, nor_13_out, nor_15_out, nor_16_out,
       nor_17_out, nor_19_out, nor_20_out, nor_21_out, nor_22_out, nor_23_out, nor_24_out, nor_25_out,
       nor_26_out, nor_27_out, nor_28_out, nor_29_out, nor_30_out, nor_31_out, nor_32_out, nor_33_out,
       nor_34_out, nor_36_out, nor_37_out, nor_38_out, nor_39_out, nor_40_out, nor_41_out, nor_43_out,
       nor_44_out, nor_45_out, nor_46_out, nor_48_out, nor_49_out, nor_50_out, nor_51_out, nor_52_out,
       nor_54_out, nor_56_out, nor_57_out, nor_58_out, nor_59_out, nor_61_out, nor_62_out, nor_63_out,
       nor_65_out, nor_66_out, nor_67_out, nor_68_out, nor_69_out, nor_70_out, nor_71_out, nor_72_out,
       nor_74_out, nor_76_out, nor_77_out, nor_78_out, nor_80_out, nor_81_out, nor_82_out, nor_83_out,
       nor_84_out, nor_85_out, nor_86_out, nor_88_out, nor_89_out, nor_90_out, nor_91_out, nor_92_out,
       nor_93_out, nor_94_out, nor_95_out, nor_96_out, nor_97_out, nor_98_out, nor_99_out, nor_100_out,
       nor_101_out, nor_103_out, nor_104_out, nor_105_out, nor_106_out, nor_107_out, nor_108_out,
       nor_109_out, nor_110_out, nor_112_out, nor_113_out, nor_114_out, nor_115_out, nor_116_out,
       nor_117_out, nor_119_out, nor_120_out, nor_122_out, nor_123_out, nor_124_out, nor_125_out,
       nor_127_out, nor_128_out, not_1_out, not_2_out, not_3_out, not_4_out, not_5_out, not_7_out, not_8_out,
       not_9_out, not_10_out, not_11_out, not_12_out, not_13_out, not_14_out, not_15_out, not_16_out,
       not_17_out, not_18_out, not_19_out, not_20_out, not_29_out, not_30_out, not_31_out, not_32_out,
       not_33_out, not_34_out, not_35_out, not_36_out, not_37_out, not_38_out, not_40_out, not_42_out,
       not_43_out, not_44_out, not_45_out, not_46_out, not_47_out, not_48_out, not_49_out, not_50_out,
       not_51_out, not_53_out, not_54_out, not_55_out, not_56_out, not_57_out, not_58_out, not_59_out,
       not_60_out, not_61_out, not_62_out, not_63_out, not_64_out, not_65_out, not_66_out, not_67_out,
       not_68_out, not_69_out, not_70_out, not_72_out, not_73_out, not_74_out, not_75_out, not_76_out,
       not_77_out, not_78_out, not_79_out, not_80_out, not_81_out, not_82_out, not_84_out, not_85_out,
       not_86_out, not_87_out, not_88_out, not_89_out, not_90_out, not_91_out, not_92_out, not_93_out,
       not_95_out, not_96_out, not_97_out, not_98_out, register_1_q, transmission_1_p4, transmission_3_p1,
       transmission_3_p3, transmission_5_p1, transmission_7_p1, transmission_9_p1, transmission_9_p2,
       transmission_9_p3, transmission_11_p4, transmission_13_p1, transmission_15_p1, transmission_17_p1,
       transmission_19_p1, transmission_19_p2, transmission_19_p3, transmission_23_p1, transmission_25_p1,
       transmission_27_p1, transmission_27_p3, transmission_29_p1, transmission_29_p2;
  wire [3:0] multiplexer_1_out, multiplexer_1_out_2, multiplexer_1_out_3, multiplexer_1_out_4,
       multiplexer_3_out, multiplexer_3_out_2, multiplexer_3_out_3, multiplexer_3_out_4, nor_5_out;
  wire [7:0] nor_35_out, nor_64_out, not_21_out;
  wire [7:4] transmission_1_p3;
  wire [15:0] multiplexer_2_out, not_6_out, R0_q, R1_q, R2_q, R3_q;

  Clock clk (.out(clk_out));
  nand nand_1 (nand_1_out, multiplexer_1_out_2[0], multiplexer_3_out_2[0]);
  not not_1 (not_1_out, Aselect[0]);
  not not_2 (not_2_out, Aselect[1]);
  not not_3 (not_3_out, Aselect[1]);
  not not_4 (not_4_out, Aselect[0]);
  Multiplexer #(.select(2), .width(16)) multiplexer_1 (
    .in0(R0_q), .in1(R1_q), .in2(R2_q), .in3(R3_q),
    .out({multiplexer_1_out_4[0], multiplexer_1_out_4[1], multiplexer_1_out_4[2], multiplexer_1_out_4[3], multiplexer_1_out_2, multiplexer_1_out_3, multiplexer_1_out}),
    .sel(Aselect));
  nor nor_1 (nor_1_out, multiplexer_1_out_2[0], multiplexer_3_out_2[0]);
  not not_5 (not_5_out, nand_1_out);
  nand nand_2 (nand_2_out, nand_1_out, nand_3_out);
  and and_1 (and_1_out, not_1_out, not_2_out, 1'b1);
  and and_2 (and_2_out, Aselect[0], not_3_out, 1'b1);
  and and_3 (and_3_out, not_4_out, Aselect[1], 1'b1);
  and and_4 (and_4_out, Aselect[0], Aselect[1], 1'b1);
  Multiplexer #(.select(2), .width(16)) multiplexer_2 (
    .in0(R0_q), .in1(R1_q), .in2(R2_q), .in3(R3_q), .out(multiplexer_2_out), .sel(Bselect));
  nor nor_2 (nor_2_out, nor_1_out, not_5_out);
  nand nand_3 (nand_3_out, 1'b0, nor_2_out);
  nand nand_4 (nand_4_out, multiplexer_1_out_2[1], multiplexer_3_out_2[1]);
  nand nand_5 (nand_5_out, nand_4_out, nand_6_out);
  assign not_6_out = ~multiplexer_2_out;  // NOT_Gate not_6, 16 bits wide
  Multiplexer #(.width(16)) multiplexer_3 (
    .in0({multiplexer_1_out_4[0], multiplexer_1_out_4[1], multiplexer_1_out_4[2], multiplexer_1_out_4[3], multiplexer_1_out_2, multiplexer_1_out_3, multiplexer_1_out}),
    .in1(not_6_out),
    .out({multiplexer_3_out_4[0], multiplexer_3_out_4[1], multiplexer_3_out_4[2], multiplexer_3_out_4[3], multiplexer_3_out_2, multiplexer_3_out_3, multiplexer_3_out}),
    .sel(Subtract));
  nor nor_3 (nor_3_out, nor_2_out, 1'b0);
  not not_7 (not_7_out, nand_3_out);
  nor nor_4 (nor_4_out, multiplexer_1_out_2[1], multiplexer_3_out_2[1]);
  not not_8 (not_8_out, nand_4_out);
  nand nand_6 (nand_6_out, nand_2_out, nor_6_out);
  nand nand_7 (nand_7_out, multiplexer_1_out_2[2], multiplexer_3_out_2[2]);
  nor nor_5 (nor_5_out[0], nor_3_out, not_7_out);
  nor nor_6 (nor_6_out, nor_4_out, not_8_out);
  not not_9 (not_9_out, nand_6_out);
  nor nor_7 (nor_7_out, multiplexer_1_out_2[2], multiplexer_3_out_2[2]);
  not not_10 (not_10_out, nand_7_out);
  nand nand_8 (nand_8_out, nand_7_out, nand_9_out);
  Register #(.width(16)) R0 (.D({not_21_out, nor_35_out}), .en(and_1_out), .clk(clk_out), .Q(R0_q), .clr(rst));
  Register #(.width(16)) R1 (.D({not_21_out, nor_35_out}), .en(and_2_out), .clk(clk_out), .Q(R1_q), .clr(rst));
  Register #(.width(16)) R2 (.D({not_21_out, nor_35_out}), .en(and_3_out), .clk(clk_out), .Q(R2_q), .clr(rst));
  Register #(.width(16)) R3 (.D({not_21_out, nor_35_out}), .en(and_4_out), .clk(clk_out), .Q(R3_q), .clr(rst));
  Multiplexer multiplexer_4 (
    .in0(multiplexer_1_out_4[0]), .in1(not_11_out), .out(multiplexer_4_out), .sel(multiplexer_3_out_4[0]));
  not not_11 (not_11_out, multiplexer_1_out_4[0]);
  nor nor_8 (nor_8_out, nor_6_out, nand_2_out);
  nor nor_9 (nor_9_out, nor_7_out, not_10_out);
  nand nand_9 (nand_9_out, nand_5_out, nor_9_out);
  nand nand_10 (nand_10_out, multiplexer_1_out_2[3], multiplexer_3_out_2[3]);
  nand nand_11 (nand_11_out, nand_10_out, nand_12_out);
  not not_12 (not_12_out, not_21_out[7]);
  not not_13 (not_13_out, multiplexer_4_out);
  nor nor_10 (nor_5_out[1], nor_8_out, not_9_out);
  nor nor_11 (nor_11_out, nor_9_out, nand_5_out);
  not not_14 (not_14_out, nand_9_out);
  nor nor_12 (nor_12_out, multiplexer_1_out_2[3], multiplexer_3_out_2[3]);
  not not_15 (not_15_out, nand_10_out);
  nand nand_12 (nand_12_out, nand_8_out, nor_15_out);
  Hex_Digit_Display hex_digit_display_1 (.value(R0_q[15:12]));  // open: dp
  Hex_Digit_Display hex_digit_display_2 (.value(R1_q[15:12]));  // open: dp
  Hex_Digit_Display hex_digit_display_3 (.value(R2_q[15:12]));  // open: dp
  Hex_Digit_Display hex_digit_display_4 (.value(R3_q[15:12]));  // open: dp
  Register #(.width(1)) register_1 (.D(1'b1), .en(and_5_out), .clk(clk_out), .Q(register_1_q), .clr(rst));
  Multiplexer multiplexer_5 (.in0(not_21_out[7]), .in1(not_12_out), .out(multiplexer_5_out), .sel(not_29_out));
  and and_5 (and_5_out, multiplexer_5_out, not_13_out);
  nor nor_13 (nor_13_out, multiplexer_3_out_4[3], multiplexer_1_out_4[3]);
  nor nor_14 (nor_5_out[2], nor_11_out, not_14_out);
  nor nor_15 (nor_15_out, nor_12_out, not_15_out);
  not not_16 (not_16_out, nand_12_out);
  Hex_Digit_Display hex_digit_display_5 (.value(R0_q[11:8]));  // open: dp
  Hex_Digit_Display hex_digit_display_6 (.value(R0_q[7:4]));  // open: dp
  Hex_Digit_Display hex_digit_display_7 (.value(R1_q[11:8]));  // open: dp
  Hex_Digit_Display hex_digit_display_8 (.value(R1_q[7:4]));  // open: dp
  Hex_Digit_Display hex_digit_display_9 (.value(R2_q[11:8]));  // open: dp
  Hex_Digit_Display hex_digit_display_10 (.value(R2_q[7:4]));  // open: dp
  Hex_Digit_Display hex_digit_display_11 (.value(R3_q[11:8]));  // open: dp
  Hex_Digit_Display hex_digit_display_12 (.value(R3_q[7:4]));  // open: dp
  LED led_1 (.in(register_1_q));
  nand nand_13 (nand_13_out, multiplexer_3_out_4[3], multiplexer_1_out_4[3]);
  nor nor_16 (nor_16_out, nor_13_out, not_17_out);
  nor nor_17 (nor_17_out, nor_15_out, nand_8_out);
  Hex_Digit_Display hex_digit_display_13 (.value(R0_q[3:0]));  // open: dp
  Hex_Digit_Display hex_digit_display_14 (.value(R1_q[3:0]));  // open: dp
  Hex_Digit_Display hex_digit_display_15 (.value(R2_q[3:0]));  // open: dp
  Hex_Digit_Display hex_digit_display_16 (.value(R3_q[3:0]));  // open: dp
  not not_17 (not_17_out, nand_13_out);
  nor nor_18 (nor_5_out[3], nor_17_out, not_16_out);
  nand nand_14 (nand_14_out, multiplexer_3_out_4[0], multiplexer_1_out_4[0]);
  nor nor_19 (nor_19_out, multiplexer_3_out_4[0], multiplexer_1_out_4[0]);
  not not_18 (not_18_out, nand_14_out);
  nand nand_15 (nand_15_out, nand_14_out, nand_16_out);
  nor nor_20 (nor_20_out, nor_19_out, not_18_out);
  nand nand_16 (nand_16_out, not_17_out, nor_20_out);
  nor nor_21 (nor_21_out, nor_20_out, not_17_out);
  not not_19 (not_19_out, nand_16_out);
  nand nand_17 (nand_17_out, multiplexer_3_out_4[1], multiplexer_1_out_4[1]);
  not not_20 (not_20_out, nand_17_out);
  nand nand_18 (nand_18_out, nand_17_out, nand_19_out);
  not not_21 (not_21_out[0], mx2i_1_z);
  mx2i mx2i_1 (.in0(nor_64_out[0]), .S(transmission_19_p2), .in1(nor_5_out[0]), .Z(mx2i_1_z));
  not not_22 (not_21_out[1], mx2i_2_z);
  mx2i mx2i_2 (.in0(nor_64_out[1]), .S(transmission_19_p2), .in1(nor_5_out[1]), .Z(mx2i_2_z));
  not not_23 (not_21_out[2], mx2i_3_z);
  mx2i mx2i_3 (.in0(nor_64_out[2]), .S(transmission_19_p2), .in1(nor_5_out[2]), .Z(mx2i_3_z));
  not not_24 (not_21_out[3], mx2i_4_z);
  mx2i mx2i_4 (.in0(nor_64_out[3]), .S(transmission_19_p2), .in1(nor_5_out[3]), .Z(mx2i_4_z));
  not not_25 (not_21_out[4], mx2i_5_z);
  mx2i mx2i_5 (.in0(nor_64_out[4]), .S(transmission_19_p2), .in1(transmission_1_p3[4]), .Z(mx2i_5_z));
  not not_26 (not_21_out[5], mx2i_6_z);
  mx2i mx2i_6 (.in0(nor_64_out[5]), .S(transmission_19_p2), .in1(transmission_1_p3[5]), .Z(mx2i_6_z));
  not not_27 (not_21_out[6], mx2i_7_z);
  mx2i mx2i_7 (.in0(nor_64_out[6]), .S(transmission_19_p2), .in1(transmission_1_p3[6]), .Z(mx2i_7_z));
  not not_28 (not_21_out[7], mx2i_8_z);
  mx2i mx2i_8 (.in0(nor_64_out[7]), .S(transmission_19_p2), .in1(transmission_1_p3[7]), .Z(mx2i_8_z));
  not not_29 (not_29_out, mx2i_9_z);
  mx2i mx2i_9 (.in0(transmission_29_p2), .S(transmission_19_p2), .in1(transmission_9_p2), .Z(mx2i_9_z));
  nor nor_22 (nor_22_out, nor_21_out, not_19_out);
  nor nor_23 (nor_23_out, multiplexer_3_out_4[1], multiplexer_1_out_4[1]);
  nor nor_24 (nor_24_out, nor_23_out, not_20_out);
  nand nand_19 (nand_19_out, nand_15_out, nor_24_out);
  not not_30 (not_30_out, nand_19_out);
  nand nand_20 (nand_20_out, multiplexer_3_out_4[2], multiplexer_1_out_4[2]);
  nor nor_25 (nor_25_out, multiplexer_3_out[0], multiplexer_1_out[0]);
  nand nand_21 (nand_21_out, multiplexer_3_out[0], multiplexer_1_out[0]);
  not not_31 (not_31_out, nand_21_out);
  nand nand_22 (nand_22_out, nand_21_out, nand_25_out);
  nand nand_23 (nand_23_out, multiplexer_3_out_4[3], multiplexer_1_out_4[3]);
  nor nor_26 (nor_26_out, nor_24_out, nand_15_out);
  nor nor_27 (nor_27_out, nor_26_out, not_30_out);
  nor nor_28 (nor_28_out, multiplexer_3_out_4[2], multiplexer_1_out_4[2]);
  not not_32 (not_32_out, nand_20_out);
  nand nand_24 (nand_24_out, nand_20_out, nand_29_out);
  nor nor_29 (nor_29_out, nor_25_out, not_31_out);
  nand nand_25 (nand_25_out, Subtract, nor_29_out);
  nand nand_26 (nand_26_out, multiplexer_3_out[1], multiplexer_1_out[1]);
  nand nand_27 (nand_27_out, nand_26_out, nand_30_out);
  nor nor_30 (nor_30_out, multiplexer_3_out_4[3], multiplexer_1_out_4[3]);
  not not_33 (not_33_out, nor_30_out);
  nand nand_28 (nand_28_out, nand_23_out, not_33_out);
  nor nor_31 (nor_31_out, nor_28_out, not_32_out);
  nand nand_29 (nand_29_out, nand_18_out, nor_31_out);
  nor nor_32 (nor_32_out, nor_29_out, Subtract);
  not not_34 (not_34_out, nand_25_out);
  nor nor_33 (nor_33_out, multiplexer_3_out[1], multiplexer_1_out[1]);
  not not_35 (not_35_out, nand_26_out);
  nor nor_34 (nor_34_out, nor_31_out, nand_18_out);
  not not_36 (not_36_out, nand_29_out);
  // Transmission_Gate transmission_1: pin names not known; wires that end beside it: nand_11_out, nand_28_out, transmission_1_p3[4], transmission_1_p4
  nor nor_35 (nor_35_out[0], nor_32_out, not_34_out);
  nor nor_36 (nor_36_out, nor_33_out, not_35_out);
  not not_37 (not_37_out, nand_30_out);
  nand nand_30 (nand_30_out, nand_22_out, nor_36_out);
  nor nor_37 (nor_37_out, multiplexer_3_out[2], multiplexer_1_out[2]);
  nand nand_31 (nand_31_out, multiplexer_3_out[2], multiplexer_1_out[2]);
  not not_38 (not_38_out, nand_31_out);
  nand nand_32 (nand_32_out, nand_31_out, nand_35_out);
  nand nand_33 (nand_33_out, multiplexer_3_out_4[0], multiplexer_1_out_4[0]);
  nand nand_34 (nand_34_out, nand_33_out, nand_38_out);
  nor nor_38 (nor_38_out, nor_34_out, not_36_out);
  not not_39 (transmission_1_p4, nand_11_out);
  // Transmission_Gate transmission_2: pin names not known; wires that end beside it: transmission_1_p4, nor_16_out, transmission_1_p3[4], nand_11_out
  // Transmission_Gate transmission_3: pin names not known; wires that end beside it: transmission_3_p1, transmission_1_p3[7], transmission_3_p3
  nor nor_39 (nor_39_out, nor_36_out, nand_22_out);
  nor nor_40 (nor_40_out, nor_37_out, not_38_out);
  nand nand_35 (nand_35_out, nand_27_out, nor_40_out);
  nand nand_36 (nand_36_out, multiplexer_3_out[3], multiplexer_1_out[3]);
  nand nand_37 (nand_37_out, nand_36_out, nand_39_out);
  nor nor_41 (nor_41_out, multiplexer_3_out_4[0], multiplexer_1_out_4[0]);
  not not_40 (not_40_out, nand_33_out);
  not not_41 (transmission_3_p3, nand_11_out);
  // Transmission_Gate transmission_4: pin names not known; wires that end beside it: transmission_3_p3, nor_22_out, transmission_1_p3[7], nand_11_out
  nor nor_42 (nor_35_out[1], nor_39_out, not_37_out);
  nor nor_43 (nor_43_out, nor_40_out, nand_27_out);
  not not_42 (not_42_out, nand_35_out);
  nor nor_44 (nor_44_out, multiplexer_3_out[3], multiplexer_1_out[3]);
  not not_43 (not_43_out, nand_36_out);
  nor nor_45 (nor_45_out, nor_41_out, not_40_out);
  not not_44 (not_44_out, nand_38_out);
  nand nand_38 (nand_38_out, not_33_out, nor_45_out);
  not not_45 (not_45_out, nand_11_out);
  // Transmission_Gate transmission_5: pin names not known; wires that end beside it: transmission_5_p1, transmission_1_p3[6], not_45_out
  // Transmission_Gate transmission_6: pin names not known; wires that end beside it: not_45_out, nor_27_out, transmission_1_p3[6], nand_11_out
  nor nor_46 (nor_46_out, multiplexer_1_out_3[0], multiplexer_3_out_3[0]);
  nor nor_47 (nor_35_out[2], nor_43_out, not_42_out);
  nor nor_48 (nor_48_out, nor_44_out, not_43_out);
  not not_46 (not_46_out, nand_39_out);
  nand nand_39 (nand_39_out, nand_32_out, nor_48_out);
  nor nor_49 (nor_49_out, nor_45_out, not_33_out);
  nor nor_50 (nor_50_out, multiplexer_3_out_4[1], multiplexer_1_out_4[1]);
  nand nand_40 (nand_40_out, multiplexer_3_out_4[1], multiplexer_1_out_4[1]);
  not not_47 (not_47_out, nand_40_out);
  nand nand_41 (nand_41_out, nand_40_out, nand_45_out);
  not not_48 (not_48_out, nand_11_out);
  // Transmission_Gate transmission_7: pin names not known; wires that end beside it: transmission_7_p1, transmission_1_p3[5], not_48_out
  nand nand_42 (nand_42_out, multiplexer_1_out_3[0], multiplexer_3_out_3[0]);
  nor nor_51 (nor_51_out, nor_46_out, not_50_out);
  nor nor_52 (nor_52_out, nor_48_out, nand_32_out);
  nand nand_43 (nand_43_out, multiplexer_1_out_2[0], multiplexer_3_out_2[0]);
  not not_49 (not_49_out, nand_43_out);
  nand nand_44 (nand_44_out, nand_43_out, nand_46_out);
  nor nor_53 (transmission_3_p1, nor_49_out, not_44_out);
  nor nor_54 (nor_54_out, nor_50_out, not_47_out);
  nand nand_45 (nand_45_out, nand_34_out, nor_54_out);
  // Transmission_Gate transmission_8: pin names not known; wires that end beside it: not_48_out, nor_38_out, transmission_1_p3[5], nand_11_out
  // Transmission_Gate transmission_9: pin names not known; wires that end beside it: transmission_9_p1, transmission_9_p2, transmission_9_p3
  not not_50 (not_50_out, nand_42_out);
  nor nor_55 (nor_35_out[3], nor_52_out, not_46_out);
  nor nor_56 (nor_56_out, multiplexer_1_out_2[0], multiplexer_3_out_2[0]);
  nor nor_57 (nor_57_out, nor_56_out, not_49_out);
  nand nand_46 (nand_46_out, 1'b1, nor_57_out);
  nand nand_47 (nand_47_out, multiplexer_1_out_2[1], multiplexer_3_out_2[1]);
  nor nor_58 (nor_58_out, nor_54_out, nand_34_out);
  not not_51 (not_51_out, nand_45_out);
  nand nand_48 (nand_48_out, multiplexer_3_out_4[2], multiplexer_1_out_4[2]);
  not not_52 (transmission_9_p3, nand_11_out);
  // Transmission_Gate transmission_10: pin names not known; wires that end beside it: transmission_9_p3, nand_24_out, transmission_9_p2, nand_11_out
  nand nand_49 (nand_49_out, multiplexer_1_out_3[3], multiplexer_3_out_3[3]);
  not not_53 (not_53_out, nand_46_out);
  nor nor_59 (nor_59_out, multiplexer_1_out_2[1], multiplexer_3_out_2[1]);
  not not_54 (not_54_out, nand_47_out);
  nand nand_50 (nand_50_out, nand_47_out, nand_53_out);
  nor nor_60 (transmission_5_p1, nor_58_out, not_51_out);
  nor nor_61 (nor_61_out, multiplexer_3_out_4[2], multiplexer_1_out_4[2]);
  not not_55 (not_55_out, nand_48_out);
  nand nand_51 (transmission_9_p1, nand_48_out, nand_56_out);
  nor nor_62 (nor_62_out, multiplexer_1_out_3[3], multiplexer_3_out_3[3]);
  not not_56 (not_56_out, nand_49_out);
  nand nand_52 (nand_52_out, nand_49_out, nand_57_out);
  nor nor_63 (nor_63_out, nor_57_out, 1'b1);
  nor nor_64 (nor_64_out[0], nor_63_out, not_53_out);
  nor nor_65 (nor_65_out, nor_59_out, not_54_out);
  nand nand_53 (nand_53_out, nand_44_out, nor_65_out);
  nand nand_54 (nand_54_out, multiplexer_1_out_2[2], multiplexer_3_out_2[2]);
  not not_57 (not_57_out, nand_54_out);
  nand nand_55 (nand_55_out, nand_54_out, nand_58_out);
  nor nor_66 (nor_66_out, nor_61_out, not_55_out);
  nand nand_56 (nand_56_out, nand_41_out, nor_66_out);
  nor nor_67 (nor_67_out, nor_62_out, not_56_out);
  nand nand_57 (nand_57_out, not_50_out, nor_67_out);
  nor nor_68 (nor_68_out, nor_65_out, nand_44_out);
  not not_58 (not_58_out, nand_53_out);
  nor nor_69 (nor_69_out, multiplexer_1_out_2[2], multiplexer_3_out_2[2]);
  nor nor_70 (nor_70_out, nor_69_out, not_57_out);
  nand nand_58 (nand_58_out, nand_50_out, nor_70_out);
  nand nand_59 (nand_59_out, multiplexer_1_out_2[3], multiplexer_3_out_2[3]);
  nor nor_71 (nor_71_out, nor_66_out, nand_41_out);
  not not_59 (not_59_out, nand_56_out);
  nor nor_72 (nor_72_out, nor_67_out, not_50_out);
  not not_60 (not_60_out, nand_57_out);
  nand nand_60 (nand_60_out, multiplexer_1_out_3[2], multiplexer_3_out_3[2]);
  nand nand_61 (nand_61_out, nand_60_out, nand_63_out);
  nor nor_73 (nor_64_out[1], nor_68_out, not_58_out);
  not not_61 (not_61_out, nand_58_out);
  nor nor_74 (nor_74_out, multiplexer_1_out_2[3], multiplexer_3_out_2[3]);
  not not_62 (not_62_out, nand_59_out);
  nand nand_62 (nand_62_out, nand_59_out, nand_64_out);
  nor nor_75 (transmission_7_p1, nor_71_out, not_59_out);
  nor nor_76 (nor_76_out, nor_72_out, not_60_out);
  nor nor_77 (nor_77_out, multiplexer_1_out_3[2], multiplexer_3_out_3[2]);
  not not_63 (not_63_out, nand_60_out);
  nand nand_63 (nand_63_out, nand_52_out, nor_81_out);
  nor nor_78 (nor_78_out, nor_70_out, nand_50_out);
  nor nor_79 (nor_64_out[2], nor_78_out, not_61_out);
  nor nor_80 (nor_80_out, nor_74_out, not_62_out);
  nand nand_64 (nand_64_out, nand_55_out, nor_80_out);
  nor nor_81 (nor_81_out, nor_77_out, not_63_out);
  not not_64 (not_64_out, nand_63_out);
  nor nor_82 (nor_82_out, multiplexer_3_out_4[3], multiplexer_1_out_4[3]);
  nand nand_65 (nand_65_out, multiplexer_3_out_4[3], multiplexer_1_out_4[3]);
  nor nor_83 (nor_83_out, nor_82_out, not_67_out);
  nor nor_84 (nor_84_out, nor_80_out, nand_55_out);
  not not_65 (not_65_out, nand_64_out);
  nand nand_66 (nand_66_out, multiplexer_1_out_3[0], multiplexer_3_out_3[0]);
  nor nor_85 (nor_85_out, nor_81_out, nand_52_out);
  nor nor_86 (nor_86_out, multiplexer_1_out_3[1], multiplexer_3_out_3[1]);
  nand nand_67 (nand_67_out, multiplexer_1_out_3[1], multiplexer_3_out_3[1]);
  not not_66 (not_66_out, nand_67_out);
  nand nand_68 (nand_68_out, nand_67_out, nand_70_out);
  not not_67 (not_67_out, nand_65_out);
  nor nor_87 (nor_64_out[3], nor_84_out, not_65_out);
  nor nor_88 (nor_88_out, multiplexer_1_out_3[0], multiplexer_3_out_3[0]);
  nand nand_69 (nand_69_out, nand_66_out, not_68_out);
  nor nor_89 (nor_89_out, nor_85_out, not_64_out);
  nor nor_90 (nor_90_out, nor_86_out, not_66_out);
  nand nand_70 (nand_70_out, nand_61_out, nor_90_out);
  not not_68 (not_68_out, nor_88_out);
  nor nor_91 (nor_91_out, nor_90_out, nand_61_out);
  not not_69 (not_69_out, nand_70_out);
  // Transmission_Gate transmission_11: pin names not known; wires that end beside it: nand_37_out, nand_69_out, nor_35_out[4], transmission_11_p4
  nor nor_92 (nor_92_out, multiplexer_3_out_4[0], multiplexer_1_out_4[0]);
  nand nand_71 (nand_71_out, multiplexer_3_out_4[0], multiplexer_1_out_4[0]);
  not not_70 (not_70_out, nand_71_out);
  nand nand_72 (nand_72_out, nand_71_out, nand_74_out);
  nand nand_73 (nand_73_out, multiplexer_1_out_3[3], multiplexer_3_out_3[3]);
  nor nor_93 (nor_93_out, nor_91_out, not_69_out);
  not not_71 (transmission_11_p4, nand_37_out);
  // Transmission_Gate transmission_12: pin names not known; wires that end beside it: transmission_11_p4, nor_51_out, nor_35_out[4], nand_37_out
  nor nor_94 (nor_94_out, nor_92_out, not_70_out);
  nand nand_74 (nand_74_out, not_67_out, nor_94_out);
  nor nor_95 (nor_95_out, multiplexer_1_out_3[3], multiplexer_3_out_3[3]);
  not not_72 (not_72_out, nand_73_out);
  nand nand_75 (nand_75_out, nand_73_out, nand_77_out);
  not not_73 (not_73_out, nand_37_out);
  // Transmission_Gate transmission_13: pin names not known; wires that end beside it: transmission_13_p1, nor_35_out[7], not_73_out
  // Transmission_Gate transmission_14: pin names not known; wires that end beside it: not_73_out, nor_76_out, nor_35_out[7], nand_37_out
  nor nor_96 (nor_96_out, nor_94_out, not_67_out);
  not not_74 (not_74_out, nand_74_out);
  nand nand_76 (nand_76_out, multiplexer_3_out_4[1], multiplexer_1_out_4[1]);
  nor nor_97 (nor_97_out, nor_95_out, not_72_out);
  nand nand_77 (nand_77_out, not_68_out, nor_97_out);
  not not_75 (not_75_out, nand_37_out);
  // Transmission_Gate transmission_15: pin names not known; wires that end beside it: transmission_15_p1, nor_35_out[6], not_75_out
  nor nor_98 (nor_98_out, nor_96_out, not_74_out);
  nor nor_99 (nor_99_out, multiplexer_3_out_4[1], multiplexer_1_out_4[1]);
  not not_76 (not_76_out, nand_76_out);
  nand nand_78 (nand_78_out, nand_76_out, nand_81_out);
  nor nor_100 (nor_100_out, nor_97_out, not_68_out);
  not not_77 (not_77_out, nand_77_out);
  nand nand_79 (nand_79_out, multiplexer_1_out_3[2], multiplexer_3_out_3[2]);
  not not_78 (not_78_out, nand_79_out);
  nand nand_80 (nand_80_out, nand_79_out, nand_82_out);
  not not_79 (not_79_out, nand_37_out);
  // Transmission_Gate transmission_16: pin names not known; wires that end beside it: not_75_out, nor_89_out, nor_35_out[6], nand_37_out
  // Transmission_Gate transmission_17: pin names not known; wires that end beside it: transmission_17_p1, nor_35_out[5], not_79_out
  nor nor_101 (nor_101_out, nor_99_out, not_76_out);
  nand nand_81 (nand_81_out, nand_72_out, nor_101_out);
  nor nor_102 (transmission_13_p1, nor_100_out, not_77_out);
  nor nor_103 (nor_103_out, multiplexer_1_out_3[2], multiplexer_3_out_3[2]);
  nor nor_104 (nor_104_out, nor_103_out, not_78_out);
  nand nand_82 (nand_82_out, nand_75_out, nor_104_out);
  // Transmission_Gate transmission_18: pin names not known; wires that end beside it: not_79_out, nor_93_out, nor_35_out[5], nand_37_out
  // Transmission_Gate transmission_19: pin names not known; wires that end beside it: transmission_19_p1, transmission_19_p2, transmission_19_p3
  nor nor_105 (nor_105_out, nor_101_out, nand_72_out);
  not not_80 (not_80_out, nand_81_out);
  nand nand_83 (nand_83_out, multiplexer_3_out_4[2], multiplexer_1_out_4[2]);
  not not_81 (not_81_out, nand_83_out);
  nand nand_84 (nand_84_out, nand_83_out, nand_88_out);
  not not_82 (not_82_out, nand_82_out);
  nand nand_85 (nand_85_out, multiplexer_1_out_3[1], multiplexer_3_out_3[1]);
  not not_83 (transmission_19_p3, nand_37_out);
  // Transmission_Gate transmission_20: pin names not known; wires that end beside it: transmission_19_p3, nand_68_out, transmission_19_p2, nand_37_out
  nand nand_86 (nand_86_out, multiplexer_3_out_4[3], multiplexer_1_out_4[3]);
  nor nor_106 (nor_106_out, multiplexer_3_out_4[3], multiplexer_1_out_4[3]);
  nand nand_87 (nand_87_out, nand_86_out, not_85_out);
  nor nor_107 (nor_107_out, nor_105_out, not_80_out);
  nor nor_108 (nor_108_out, multiplexer_3_out_4[2], multiplexer_1_out_4[2]);
  nor nor_109 (nor_109_out, nor_108_out, not_81_out);
  nand nand_88 (nand_88_out, nand_78_out, nor_109_out);
  nor nor_110 (nor_110_out, nor_104_out, nand_75_out);
  nor nor_111 (transmission_15_p1, nor_110_out, not_82_out);
  nor nor_112 (nor_112_out, multiplexer_1_out_3[1], multiplexer_3_out_3[1]);
  not not_84 (not_84_out, nand_85_out);
  nand nand_89 (transmission_19_p1, nand_85_out, nand_90_out);
  not not_85 (not_85_out, nor_106_out);
  not not_86 (not_86_out, nand_88_out);
  nor nor_113 (nor_113_out, nor_112_out, not_84_out);
  nand nand_90 (nand_90_out, nand_80_out, nor_113_out);
  nand nand_91 (nand_91_out, multiplexer_3_out_4[0], multiplexer_1_out_4[0]);
  nor nor_114 (nor_114_out, nor_109_out, nand_78_out);
  nor nor_115 (nor_115_out, nor_114_out, not_86_out);
  not not_87 (not_87_out, nand_62_out);
  // Transmission_Gate transmission_21: pin names not known; wires that end beside it: nand_62_out, nand_87_out, nor_64_out[4], not_87_out
  // Transmission_Gate transmission_22: pin names not known; wires that end beside it: not_87_out, nor_83_out, nor_64_out[4], nand_62_out
  nor nor_116 (nor_116_out, nor_113_out, nand_80_out);
  not not_88 (not_88_out, nand_90_out);
  nor nor_117 (nor_117_out, multiplexer_3_out_4[0], multiplexer_1_out_4[0]);
  not not_89 (not_89_out, nand_91_out);
  nand nand_92 (nand_92_out, nand_91_out, nand_93_out);
  not not_90 (not_90_out, nand_62_out);
  // Transmission_Gate transmission_23: pin names not known; wires that end beside it: transmission_23_p1, nor_64_out[7], not_90_out
  nor nor_118 (transmission_17_p1, nor_116_out, not_88_out);
  nor nor_119 (nor_119_out, nor_117_out, not_89_out);
  nand nand_93 (nand_93_out, not_85_out, nor_119_out);
  not not_91 (not_91_out, nand_62_out);
  // Transmission_Gate transmission_24: pin names not known; wires that end beside it: not_90_out, nor_98_out, nor_64_out[7], nand_62_out
  // Transmission_Gate transmission_25: pin names not known; wires that end beside it: transmission_25_p1, nor_64_out[6], not_91_out
  nor nor_120 (nor_120_out, nor_119_out, not_85_out);
  not not_92 (not_92_out, nand_93_out);
  nand nand_94 (nand_94_out, multiplexer_3_out_4[1], multiplexer_1_out_4[1]);
  nand nand_95 (nand_95_out, nand_94_out, nand_96_out);
  // Transmission_Gate transmission_26: pin names not known; wires that end beside it: not_91_out, nor_107_out, nor_64_out[6], nand_62_out
  // Transmission_Gate transmission_27: pin names not known; wires that end beside it: transmission_27_p1, nor_64_out[5], transmission_27_p3
  nor nor_121 (transmission_23_p1, nor_120_out, not_92_out);
  nor nor_122 (nor_122_out, multiplexer_3_out_4[1], multiplexer_1_out_4[1]);
  not not_93 (not_93_out, nand_94_out);
  not not_94 (transmission_27_p3, nand_62_out);
  // Transmission_Gate transmission_28: pin names not known; wires that end beside it: transmission_27_p3, nor_115_out, nor_64_out[5], nand_62_out
  nor nor_123 (nor_123_out, nor_122_out, not_93_out);
  not not_95 (not_95_out, nand_96_out);
  nand nand_96 (nand_96_out, nand_92_out, nor_123_out);
  not not_96 (not_96_out, nand_62_out);
  // Transmission_Gate transmission_29: pin names not known; wires that end beside it: transmission_29_p1, transmission_29_p2, not_96_out
  // Transmission_Gate transmission_30: pin names not known; wires that end beside it: not_96_out, nand_84_out, transmission_29_p2, nand_62_out
  nor nor_124 (nor_124_out, nor_123_out, nand_92_out);
  nor nor_125 (nor_125_out, multiplexer_3_out_4[2], multiplexer_1_out_4[2]);
  nand nand_97 (nand_97_out, multiplexer_3_out_4[2], multiplexer_1_out_4[2]);
  not not_97 (not_97_out, nand_97_out);
  nand nand_98 (transmission_29_p1, nand_97_out, nand_99_out);
  nor nor_126 (transmission_25_p1, nor_124_out, not_95_out);
  nor nor_127 (nor_127_out, nor_125_out, not_97_out);
  nand nand_99 (nand_99_out, nand_95_out, nor_127_out);
  nor nor_128 (nor_128_out, nor_127_out, nand_95_out);
  not not_98 (not_98_out, nand_99_out);
  nor nor_129 (transmission_27_p1, nor_128_out, not_98_out);

  // Notes on the sheet:
  //   FAopt1
  //   FAopt1
  //   FAopt1
  //   FA0
  //   FAopt1
  //   4bit C0
  //   FAopt1
  //   FA1
  //   FAopt1
  //   4bit c1
  //   FAopt1
  //   FAopt1
  //   FAopt1
  //   FAopt1
  //   FA0
  //   FAopt1
  //   FAopt1
  //   FAopt1
  //   4bit C0
  //   FAopt1
  //   FAopt1
  //   FAopt1
  //   FAopt1
  //   FAopt1
  //   FA0
  //   FAopt1
  //   FA1
  //   FAopt1
  //   4bit c1
  //   4bit C0
  //   FAopt1
  //   FAopt1
  //   FAopt1
  //   FA1
  //   FAopt1
  //   FAopt1
  //   4bit c1
  //   FAopt1
  //   FAopt1
  //   FAopt1
  //   FAopt1
  //   FAopt1
endmodule
